// Logisim project 000_Decoder.circ as structural Verilog: 2 circuits, main circuit main
module main (
  input  x2,
  input  x1,
  input  e,
  input  x2_2,
  input  x1_2,
  input  Enable,
  input  [1:0] Input,
  input  [1:0] in_8,
  input  x0,
  input  x1_3,
  input  e_2,
  input  x0_2,
  input  x1_4,
  input  e_3,
  input  x2_3,
  input  x3,
  output y1,
  output y1_2,
  output y2,
  output y2_2,
  output y3,
  output y3_2,
  output y4,
  output y4_2,
  output [3:0] out_25,
  output [3:0] Output,
  output out_27,
  output out_28,
  output out_29,
  output out_30,
  output y0,
  output y1_3,
  output y2_3,
  output y3_3,
  output y4_3,
  output y5,
  output y6,
  output y7,
  output y8,
  output y9,
  output y10,
  output y11,
  output y12,
  output y13,
  output y14,
  output y15
);

  wire n2_bit_decoder_2_y1, n2_bit_decoder_2_y2, n2_bit_decoder_2_y3, n2_bit_decoder_2_y4, not_1_out,
       not_2_out, not_3_out, not_4_out, not_5_out, not_6_out;

  not not_1 (not_1_out, x1);
  not not_2 (not_2_out, x2);
  and and_1 (out_25[0], not_3_out, not_4_out);
  and and_2 (out_25[1], not_3_out, in_8[0]);
  and and_3 (out_25[2], in_8[1], not_4_out);
  and and_4 (out_25[3], in_8[1], in_8[0]);
  not not_3 (not_3_out, in_8[1]);
  not not_4 (not_4_out, in_8[0]);
  and and_5 (y1, not_2_out, not_1_out);
  and and_6 (y2, not_2_out, x1);
  and and_7 (y3, x2, not_1_out);
  and and_8 (y4, x2, x1);
  not not_5 (not_5_out, x2_2);
  and and_9 (y1_2, not_5_out, e, not_6_out);
  and and_10 (y2_2, not_5_out, e, x1_2);
  and and_11 (y3_2, x2_2, e, not_6_out);
  and and_12 (y4_2, x2_2, e, x1_2);
  not not_6 (not_6_out, x1_2);
  Decoder #(.select(2)) decoder_1 (
    .out0(Output[0]), .out1(Output[1]), .out2(Output[2]), .out3(Output[3]), .sel(Input), .en(Enable));
  _2_bit_Decoder u_2_bit_decoder_1 (.x1(x0), .x2(x1_3), .e(e_2), .y1(out_27), .y2(out_28), .y3(out_29), .y4(out_30));
  _2_bit_Decoder u_2_bit_decoder_2 (
    .x1(x0_2), .x2(x1_4), .e(e_3), .y1(n2_bit_decoder_2_y1), .y2(n2_bit_decoder_2_y2),
    .y3(n2_bit_decoder_2_y3), .y4(n2_bit_decoder_2_y4));
  _2_bit_Decoder u_2_bit_decoder_3 (
    .x1(x2_3), .x2(x3), .e(n2_bit_decoder_2_y1), .y1(y0), .y2(y1_3), .y3(y2_3), .y4(y3_3));
  _2_bit_Decoder u_2_bit_decoder_4 (.x1(x2_3), .x2(x3), .e(n2_bit_decoder_2_y2), .y1(y4_3), .y2(y5), .y3(y6), .y4(y7));
  _2_bit_Decoder u_2_bit_decoder_5 (.x1(x2_3), .x2(x3), .e(n2_bit_decoder_2_y3), .y1(y8), .y2(y9), .y3(y10), .y4(y11));
  _2_bit_Decoder u_2_bit_decoder_6 (
    .x1(x2_3), .x2(x3), .e(n2_bit_decoder_2_y4), .y1(y12), .y2(y13), .y3(y14), .y4(y15));

  // Notes on the sheet:
  //   2-bit Decoder
  //   Using a Bus
  //   Individual Inputs
  //   y1=(x1)' * (x2)'
  //   y2=x1 * (x2)'
  //   y3=(x1)' * x2
  //   y4=x1 * x2
  //   Decoder: (Binary-Enoding) -> (One-Hot-Encoding)
  //   with Enable
  //   LogiSims 2-bit-Decoder
  //   Custom Sub-Circuit
  //   y1=(x1)' * (x2)'
  //   y2=x1 * (x2)'
  //   y3=(x1)' * x2
  //   y4=x1 * x2
  //   4-bit-Decoder by Chaining 2-bit-Decoders
endmodule

module _2_bit_Decoder (
  input  x1,
  input  x2,
  input  e,
  output y1,
  output y2,
  output y3,
  output y4
);

  wire not_1_out, not_2_out;

  and and_1 (y1, not_2_out, e, not_1_out);
  and and_2 (y2, not_2_out, e, x1);
  and and_3 (y3, x2, e, not_1_out);
  and and_4 (y4, x2, e, x1);
  not not_1 (not_1_out, x1);
  not not_2 (not_2_out, x2);

  // Notes on the sheet:
  //   y2=x1 * (x2)'
  //   y3=(x1)' * x2
  //   y4=x1 * x2
  //   y1=(x1)' * (x2)'
endmodule
