// Logisim project 000_Decoder_and_MUX.circ as structural Verilog: 2 circuits, main circuit main
module main (
  input  i0,
  input  i1,
  input  i0_2,
  input  i2,
  input  i1_2,
  input  i3,
  input  x2,
  input  x1,
  input  s,
  input  s1,
  input  s0,
  input  [3:0] in_12,
  input  [1:0] in_13,
  input  s_2,
  input  [1:0] in_15,
  input  [1:0] in_16,
  input  in_17,
  input  in_18,
  input  in_19,
  output y1,
  output y2,
  output y3,
  output out_23,
  output out_24,
  output y4,
  output out_26,
  output [3:0] out_27,
  output out_28,
  output out_29,
  output out_30,
  output out_31
);

  wire and_9_out, and_10_out, and_11_out, and_12_out, and_13_out, and_14_out, and_15_out, and_16_out,
       and_17_out, and_18_out, and_19_out, and_20_out, clock_1_out, not_1_out, not_2_out, not_3_out,
       not_4_out, not_5_out, not_6_out, not_7_out, not_8_out, not_9_out, not_10_out;

  Clock clock_1 (.out(clock_1_out));
  not not_1 (not_1_out, x2);
  not not_2 (not_2_out, x1);
  and and_1 (out_27[0], not_4_out, not_3_out);
  and and_2 (out_27[1], not_4_out, in_16[0]);
  and and_3 (out_27[2], in_16[1], not_3_out);
  and and_4 (out_27[3], in_16[1], in_16[0]);
  not not_3 (not_3_out, in_16[0]);
  not not_4 (not_4_out, in_16[1]);
  D_Flip_Flop d_ff_1 (.clk(in_17), .D(in_18), .Q(out_29));  // open: Qn, preset, en, reset
  D_Flip_Flop d_ff_2 (.clk(clock_1_out), .D(in_19), .Q(out_30));  // open: Qn, preset, en, reset
  and and_5 (y1, not_1_out, not_2_out);
  and and_6 (y2, not_1_out, x1);
  and and_7 (y3, x2, not_2_out);
  and and_8 (y4, x2, x1);
  D_Flip_Flop d_ff_3 (.clk(clock_1_out), .D(in_19), .Q(out_31));  // open: Qn, preset, en, reset
  and and_9 (and_9_out, i0_2, not_5_out);
  and and_10 (and_10_out, i1_2, s);
  not not_5 (not_5_out, s);
  and and_11 (and_11_out, in_13[0], not_6_out);
  and and_12 (and_12_out, in_13[1], s_2);
  not not_6 (not_6_out, s_2);
  or or_1 (out_24, and_9_out, and_10_out);
  or or_2 (out_28, and_11_out, and_12_out);
  not not_7 (not_7_out, s1);
  not not_8 (not_8_out, s0);
  not not_9 (not_9_out, in_15[1]);
  not not_10 (not_10_out, in_15[0]);
  and and_13 (and_13_out, i0, not_7_out, not_8_out);
  and and_14 (and_14_out, i1, not_7_out, s0);
  and and_15 (and_15_out, i2, s1, not_8_out);
  and and_16 (and_16_out, i3, s1, s0);
  and and_17 (and_17_out, in_12[0], not_9_out, not_10_out);
  and and_18 (and_18_out, in_12[1], not_9_out, in_15[0]);
  and and_19 (and_19_out, in_12[2], in_15[1], not_10_out);
  and and_20 (and_20_out, in_12[3], in_15[1], in_15[0]);
  or or_3 (out_23, and_13_out, and_14_out, and_15_out, and_16_out);
  or or_4 (out_26, and_17_out, and_18_out, and_19_out, and_20_out);

  // Notes on the sheet:
  //   2-bit Decoder
  //   y1=(x1)' * (x2)'
  //   y2=x1 * (x2)'
  //   y3=(x1)' * x2
  //   y4=x1 * x2
  //   2x1 MUX
  //   Using a Bus and Spitter
  //   Individual Inputs
  //   d=[i0 * (s0)'] + [i1 * s0]
  //   4x1 MUX
endmodule

module _2_bit_Decoder (
  input  x1,
  input  x2,
  output y1,
  output y2,
  output y3,
  output y4
);

  wire not_1_out, not_2_out, not_3_out, not_4_out;

  not not_1 (not_1_out, x1);
  not not_2 (not_2_out, x2);
  not not_3 (not_3_out, x1);
  not not_4 (not_4_out, x2);
  and and_1 (y4, x1, x2);
  and and_2 (y1, not_1_out, not_2_out);
  and and_3 (y2, not_3_out, x2);
  and and_4 (y3, x1, not_4_out);
endmodule
