// Logisim project 001_MUX.circ as structural Verilog: 3 circuits, main circuit main
module main (
  input  i0,
  input  i1,
  input  i0_2,
  input  i2,
  input  i1_2,
  input  i3,
  input  s,
  input  s1,
  input  s0,
  input  [3:0] in_10,
  input  [1:0] in_11,
  input  s_2,
  input  [1:0] in_13,
  input  [1:0] in_14,
  input  [3:0] in_15,
  input  s_3,
  input  [1:0] in_17,
  input  in_18,
  input  in_19,
  input  in_20,
  input  i0_3,
  input  i0_4,
  input  i1_3,
  input  i1_4,
  input  i2_2,
  input  i3_2,
  input  [1:0] select,
  input  s_4,
  output out_29,
  output out_30,
  output out_31,
  output out_32,
  output out_33,
  output out_34,
  output out_35,
  output out_36,
  output d,
  output d_2
);

  wire and_1_out, and_2_out, and_3_out, and_4_out, and_5_out, and_6_out, and_7_out, and_8_out, and_9_out,
       and_10_out, and_11_out, and_12_out, clock_1_out, n2x1_mux_2_d, n2x1_mux_3_d, not_1_out, not_2_out,
       not_3_out, not_4_out, not_5_out, not_6_out;

  not not_1 (not_1_out, s);
  and and_1 (and_1_out, in_11[0], not_2_out);
  and and_2 (and_2_out, in_11[1], s_2);
  not not_2 (not_2_out, s_2);
  _2x1_MUX u_2x1_mux_1 (.i0(in_14[0]), .i1(in_14[1]), .d(out_34), .s(s_3));
  and and_3 (and_3_out, i0_2, not_1_out);
  or or_1 (out_30, and_3_out, and_4_out);
  and and_4 (and_4_out, i1_2, s);
  or or_2 (out_31, and_1_out, and_2_out);
  Clock clock_1 (.out(clock_1_out));
  _2x1_MUX u_2x1_mux_2 (.i0(out_35), .i1(in_18), .d(n2x1_mux_2_d), .s(in_20));
  D_Flip_Flop d_ff_1 (.clk(clock_1_out), .D(n2x1_mux_2_d), .Q(out_35));  // open: Qn, preset, en, reset
  _2x1_MUX u_2x1_mux_3 (.i0(out_36), .i1(in_19), .d(n2x1_mux_3_d), .s(in_20));
  D_Flip_Flop d_ff_2 (.clk(clock_1_out), .D(n2x1_mux_3_d), .Q(out_36));  // open: Qn, preset, en, reset
  Multiplexer #(.enable("false")) multiplexer_1 (.in0(i0_4), .in1(i1_4), .out(d_2), .sel(s_4));
  not not_3 (not_3_out, s1);
  not not_4 (not_4_out, in_13[1]);
  and and_5 (and_5_out, i0, not_3_out, not_5_out);
  and and_6 (and_6_out, i1, not_3_out, s0);
  and and_7 (and_7_out, i2, s1, not_5_out);
  and and_8 (and_8_out, i3, s1, s0);
  not not_5 (not_5_out, s0);
  and and_9 (and_9_out, in_10[0], not_4_out, not_6_out);
  and and_10 (and_10_out, in_10[1], not_4_out, in_13[0]);
  and and_11 (and_11_out, in_10[2], in_13[1], not_6_out);
  and and_12 (and_12_out, in_10[3], in_13[1], in_13[0]);
  not not_6 (not_6_out, in_13[0]);
  _4x1_MUX u_4x1_mux_1 (
    .i0(in_15[0]), .i1(in_15[1]), .i2(in_15[2]), .i3(in_15[3]), .d(out_33), .s1(in_17[1]), .s0(in_17[0]));
  or or_3 (out_29, and_5_out, and_6_out, and_7_out, and_8_out);
  or or_4 (out_32, and_9_out, and_10_out, and_11_out, and_12_out);
  Multiplexer #(.select(2), .enable("false")) multiplexer_2 (
    .in0(i0_3), .in1(i1_3), .in2(i2_2), .in3(i3_2), .out(d), .sel(select));

  // Notes on the sheet:
  //   2x1 MUX
  //   d=[i0 * (s0)'] + [i1 * s0]
  //   Using a Bus
  //   Using Sub-Circuits
  //   Individual Inputs
  //   Application of 2x1-MUX in a Parallel-Load Register
  //   Built-In 2x1 MUX
  //   4x1 MUX
  //   Built-In 4x1 MUX
endmodule

module _2x1_MUX (
  input  i0,
  input  i1,
  input  s,
  output d
);

  wire and_1_out, and_2_out, not_1_out;

  not not_1 (not_1_out, s);
  and and_1 (and_1_out, i0, not_1_out);
  and and_2 (and_2_out, i1, s);
  or or_1 (d, and_1_out, and_2_out);

  // Notes on the sheet:
  //   d=[i0 * (s0)'] + [i1 * s0]
endmodule

module _4x1_MUX (
  input  i0,
  input  i1,
  input  i2,
  input  i3,
  input  s1,
  input  s0,
  output d
);

  wire and_1_out, and_2_out, and_3_out, and_4_out, not_1_out, not_2_out;

  not not_1 (not_1_out, s1);
  and and_1 (and_1_out, i0, not_1_out, not_2_out);
  and and_2 (and_2_out, i1, not_1_out, s0);
  and and_3 (and_3_out, i2, s1, not_2_out);
  and and_4 (and_4_out, i3, s1, s0);
  not not_2 (not_2_out, s0);
  or or_1 (d, and_1_out, and_2_out, and_3_out, and_4_out);
endmodule
