// Logisim project 200_Register_Parallel-Load.circ as structural Verilog: 5 circuits, main circuit main
module main (
  input  in_1,
  input  in_2,
  input  in_3,
  input  in_4,
  input  in_5,
  input  in_6,
  input  in_7,
  input  in_8,
  input  in_9,
  input  in_10,
  input  in_11,
  input  in_12,
  input  in_13,
  input  in_14,
  input  in_15,
  input  in_16,
  input  in_17,
  input  in_18,
  input  in_19,
  input  in_20,
  input  in_21,
  input  in_22,
  input  [3:0] in_23,
  input  [1:0] in_24,
  input  in_25,
  input  in_26,
  output out_27,
  output out_28,
  output out_29,
  output out_30,
  output out_31,
  output out_32,
  output out_33,
  output out_34,
  output out_35,
  output out_36,
  output out_37,
  output out_38,
  output out_39,
  output out_40,
  output [1:0] out_41,
  output [3:0] out_42,
  output [1:0] out_43,
  output [3:0] out_44
);

  wire clock_1_out, clock_2_out, clock_3_out, clock_4_out, clock_5_out, clock_6_out, clock_7_out,
       clock_8_out, multiplexer_1_out, multiplexer_2_out, multiplexer_4_out, multiplexer_5_out,
       multiplexer_6_out, multiplexer_7_out, n2x1_mux_1_d, n2x1_mux_2_d, n2x1_mux_4_d, n2x1_mux_5_d,
       n2x1_mux_6_d, n2x1_mux_7_d, not_1_out, not_2_out, not_3_out, not_4_out, not_5_out;

  not not_1 (not_1_out, in_18);
  Clock clock_1 (.out(clock_1_out));
  _2x1_MUX u_2x1_mux_1 (.i0(out_32), .i1(in_5), .d(n2x1_mux_1_d), .s(in_10));
  Clock clock_2 (.out(clock_2_out));
  Multiplexer multiplexer_1 (.in0(in_12), .in1(out_35), .out(multiplexer_1_out), .sel(not_1_out), .en(1'b1));
  Clock clock_3 (.out(clock_3_out));
  not not_2 (not_2_out, in_26);
  _2x1_MUX u_2x1_mux_2 (.i0(out_33), .i1(in_6), .d(n2x1_mux_2_d), .s(in_10));
  D_Flip_Flop d_ff_1 (.clk(clock_2_out), .D(n2x1_mux_1_d), .Q(out_32));  // open: Qn, preset, en, reset
  Multiplexer multiplexer_2 (.in0(in_13), .in1(out_36), .out(multiplexer_2_out), .sel(not_1_out), .en(1'b1));
  D_Flip_Flop d_ff_2 (.clk(clock_1_out), .D(multiplexer_1_out), .Q(out_35));  // open: Qn, preset, en, reset
  _2_bit_Parallel_Load_Reg u_2_bit_parallel_load_reg_1 (
    .i1(in_24[1]), .i0(in_24[0]), .load(in_26), .q1(out_41[1]), .q0(out_41[0]), .clk(clock_3_out));
  D_Flip_Flop d_ff_3 (.clk(clock_2_out), .D(n2x1_mux_2_d), .Q(out_33));  // open: Qn, preset, en, reset
  D_Flip_Flop d_ff_4 (.clk(clock_1_out), .D(multiplexer_2_out), .Q(out_36));  // open: Qn, preset, en, reset
  Register #(.width(2)) register_1 (.D(in_24), .Q(out_43), .clk(clock_4_out), .clr(not_2_out));  // open: en
  Clock clock_4 (.out(clock_4_out));
  not not_3 (not_3_out, in_22);
  Multiplexer multiplexer_3 (.in0(in_20), .in1(in_21), .out(out_34), .sel(not_3_out), .en(1'b1));
  _2x1_MUX u_2x1_mux_3 (.i0(in_8), .i1(in_7), .d(out_27), .s(in_11));
  Clock clock_5 (.out(clock_5_out));
  not not_4 (not_4_out, in_19);
  Clock clock_6 (.out(clock_6_out));
  _2x1_MUX u_2x1_mux_4 (.i0(out_28), .i1(in_1), .d(n2x1_mux_4_d), .s(in_9));
  D_Flip_Flop d_ff_5 (.clk(clock_5_out), .D(n2x1_mux_4_d), .Q(out_28));  // open: Qn, preset, en, reset
  Multiplexer multiplexer_4 (.in0(in_14), .in1(out_37), .out(multiplexer_4_out), .sel(not_4_out), .en(1'b1));
  Clock clock_7 (.out(clock_7_out));
  not not_5 (not_5_out, in_25);
  _2x1_MUX u_2x1_mux_5 (.i0(out_29), .i1(in_2), .d(n2x1_mux_5_d), .s(in_9));
  D_Flip_Flop d_ff_6 (.clk(clock_5_out), .D(n2x1_mux_5_d), .Q(out_29));  // open: Qn, preset, en, reset
  Multiplexer multiplexer_5 (.in0(in_15), .in1(out_38), .out(multiplexer_5_out), .sel(not_4_out), .en(1'b1));
  D_Flip_Flop d_ff_7 (.clk(clock_6_out), .D(multiplexer_4_out), .Q(out_37));  // open: Qn, preset, en, reset
  _2x1_MUX u_2x1_mux_6 (.i0(out_30), .i1(in_3), .d(n2x1_mux_6_d), .s(in_9));
  D_Flip_Flop d_ff_8 (.clk(clock_5_out), .D(n2x1_mux_6_d), .Q(out_30));  // open: Qn, preset, en, reset
  Multiplexer multiplexer_6 (.in0(in_16), .in1(out_39), .out(multiplexer_6_out), .sel(not_4_out), .en(1'b1));
  D_Flip_Flop d_ff_9 (.clk(clock_6_out), .D(multiplexer_5_out), .Q(out_38));  // open: Qn, preset, en, reset
  _4_bit_Parallel_Load_Reg u_4_bit_parallel_load_reg_1 (
    .load(in_25), .i3(in_23[3]), .i2(in_23[2]), .i1(in_23[1]), .i0(in_23[0]), .q3(out_42[3]), .q2(out_42[2]),
    .q1(out_42[1]), .q0(out_42[0]), .clk(clock_7_out));
  Register #(.width(4)) register_2 (.D(in_23), .Q(out_44), .clk(clock_8_out), .clr(not_5_out));  // open: en
  Clock clock_8 (.out(clock_8_out));
  _2x1_MUX u_2x1_mux_7 (.i0(out_31), .i1(in_4), .d(n2x1_mux_7_d), .s(in_9));
  Multiplexer multiplexer_7 (.in0(in_17), .in1(out_40), .out(multiplexer_7_out), .sel(not_4_out), .en(1'b1));
  D_Flip_Flop d_ff_10 (.clk(clock_6_out), .D(multiplexer_6_out), .Q(out_39));  // open: Qn, preset, en, reset
  D_Flip_Flop d_ff_11 (.clk(clock_5_out), .D(n2x1_mux_7_d), .Q(out_31));  // open: Qn, preset, en, reset
  D_Flip_Flop d_ff_12 (.clk(clock_6_out), .D(multiplexer_7_out), .Q(out_40));  // open: Qn, preset, en, reset

  // Notes on the sheet:
  //   2-bit Parallel-Load Register
  //   Using Custom 2x1 MUX
  //   Logisims Parallel-Load Register Sub-Circuit
  //   Custom Parallel-Load Register Sub-Circuit
  //   4-bit Parallel-Load Register
endmodule

module _2x1_MUX (
  input  i0,
  input  i1,
  input  s,
  output d
);

  wire and_1_out, and_2_out, not_1_out;

  not not_1 (not_1_out, s);
  and and_1 (and_1_out, i0, not_1_out);
  and and_2 (and_2_out, i1, s);
  or or_1 (d, and_1_out, and_2_out);

  // Notes on the sheet:
  //   d=[i0 * (s0)'] + [i1 * s0]
endmodule

module _4x1_MUX (
  input  i0,
  input  i1,
  input  i2,
  input  i3,
  input  s1,
  input  s0,
  output d
);

  wire and_1_out, and_2_out, and_3_out, and_4_out, not_1_out, not_2_out;

  not not_1 (not_1_out, s1);
  and and_1 (and_1_out, i0, not_1_out, not_2_out);
  and and_2 (and_2_out, i1, not_1_out, s0);
  and and_3 (and_3_out, i2, s1, not_2_out);
  and and_4 (and_4_out, i3, s1, s0);
  not not_2 (not_2_out, s0);
  or or_1 (d, and_1_out, and_2_out, and_3_out, and_4_out);
endmodule

module _2_bit_Parallel_Load_Reg (
  input  i1,
  input  i0,
  input  load,
  input  clk,
  output q1,
  output q0
);

  wire multiplexer_1_out, multiplexer_2_out, not_1_out;

  not not_1 (not_1_out, load);
  Multiplexer multiplexer_1 (.in0(i1), .in1(q1), .out(multiplexer_1_out), .sel(not_1_out), .en(1'b1));
  Multiplexer multiplexer_2 (.in0(i0), .in1(q0), .out(multiplexer_2_out), .sel(not_1_out), .en(1'b1));
  D_Flip_Flop d_ff_1 (.clk(clk), .D(multiplexer_1_out), .Q(q1));  // open: Qn, preset, en, reset
  D_Flip_Flop d_ff_2 (.clk(clk), .D(multiplexer_2_out), .Q(q0));  // open: Qn, preset, en, reset

  // Notes on the sheet:
  //   2-bit Parallel-Load Register
endmodule

module _4_bit_Parallel_Load_Reg (
  input  i3,
  input  i2,
  input  i1,
  input  i0,
  input  load,
  input  clk,
  output q3,
  output q2,
  output q1,
  output q0
);

  wire multiplexer_1_out, multiplexer_2_out, multiplexer_3_out, multiplexer_4_out, not_1_out;

  not not_1 (not_1_out, load);
  Multiplexer multiplexer_1 (.in0(i3), .in1(q3), .out(multiplexer_1_out), .sel(not_1_out), .en(1'b1));
  Multiplexer multiplexer_2 (.in0(i2), .in1(q2), .out(multiplexer_2_out), .sel(not_1_out), .en(1'b1));
  D_Flip_Flop d_ff_1 (.clk(clk), .D(multiplexer_1_out), .Q(q3));  // open: Qn, preset, en, reset
  Multiplexer multiplexer_3 (.in0(i1), .in1(q1), .out(multiplexer_3_out), .sel(not_1_out), .en(1'b1));
  D_Flip_Flop d_ff_2 (.clk(clk), .D(multiplexer_2_out), .Q(q2));  // open: Qn, preset, en, reset
  Multiplexer multiplexer_4 (.in0(i0), .in1(q0), .out(multiplexer_4_out), .sel(not_1_out), .en(1'b1));
  D_Flip_Flop d_ff_3 (.clk(clk), .D(multiplexer_3_out), .Q(q1));  // open: Qn, preset, en, reset
  D_Flip_Flop d_ff_4 (.clk(clk), .D(multiplexer_4_out), .Q(q0));  // open: Qn, preset, en, reset

  // Notes on the sheet:
  //   4-bit Parallel-Load Register
endmodule
