// Logisim project 300_Registe-File_toy.circ as structural Verilog: 2 circuits, main circuit main
module main (
  input  [1:0] write_register,
  input  [7:0] Data,
  input  write_enable,
  output [7:0] reg_1_val,
  output [7:0] reg_2_val,
  output [7:0] reg_3_val
);

  wire clk, reg1_on_off, reg2_on_off, reg3_on_off;

  Clock clock_1 (.out(clk));
  Demultiplexer #(.select(2), .enable("false")) demultiplexer_1 (
    .out1(reg1_on_off), .out2(reg2_on_off), .out3(reg3_on_off), .in(write_enable), .sel(write_register));  // open: out0
  \reg  reg_1 (.in_1(Data), .reg_on_off(reg1_on_off), .out_3(reg_1_val));
  \reg  reg_2 (.in_1(Data), .reg_on_off(reg2_on_off), .out_3(reg_2_val));
  \reg  reg_3 (.in_1(Data), .reg_on_off(reg3_on_off), .out_3(reg_3_val));

  // Other names for the same wires on the sheet: reg1_out[7:0] = reg_1_val; reg2_out[7:0] = reg_2_val;
  //   reg3_out[7:0] = reg_3_val; write_data[7:0] = Data; write_en = write_enable; write_reg[1:0] = write_register
endmodule

module \reg  (
  input  [7:0] in_1,
  input  reg_on_off,
  output [7:0] out_3
);

  wire clk_out;

  Register \reg  (.D(in_1), .en(reg_on_off), .clk(clk_out), .Q(out_3));  // open: clr
  Clock clk (.out(clk_out));
endmodule
