// Logisim project 301_Register-File_MIPS.circ as structural Verilog
module \reg  (
  input  [31:0] D,
  input  reg_on_off,
  output [31:0] Q
);

  wire clk_out;

  Register #(.width(32)) \reg  (.D(D), .en(reg_on_off), .clk(clk_out), .Q(Q));  // open: clr
  Clock clk (.out(clk_out));
endmodule

module regs (
  input  [31:0] write_data,
  input  reg01_on_off,
  input  reg02_on_off,
  input  reg03_on_off,
  input  reg04_on_off,
  input  reg05_on_off,
  input  reg06_on_off,
  input  reg07_on_off,
  input  reg08_on_off,
  input  reg09_on_off,
  input  reg10_on_off,
  input  reg11_on_off,
  input  reg12_on_off,
  input  reg13_on_off,
  input  reg14_on_off,
  input  reg15_on_off,
  input  reg16_on_off,
  input  reg17_on_off,
  input  reg18_on_off,
  input  reg19_on_off,
  input  reg20_on_off,
  input  reg21_on_off,
  input  reg22_on_off,
  input  reg23_on_off,
  input  reg24_on_off,
  input  reg25_on_off,
  input  reg26_on_off,
  input  reg27_on_off,
  input  reg28_on_off,
  input  reg29_on_off,
  input  reg30_on_off,
  input  reg31_on_off,
  output [31:0] reg01_out,
  output [31:0] reg02_out,
  output [31:0] reg03_out,
  output [31:0] reg04_out,
  output [31:0] reg05_out,
  output [31:0] reg06_out,
  output [31:0] reg07_out,
  output [31:0] reg08_out,
  output [31:0] reg09_out,
  output [31:0] reg10_out,
  output [31:0] reg11_out,
  output [31:0] reg12_out,
  output [31:0] reg13_out,
  output [31:0] reg14_out,
  output [31:0] reg15_out,
  output [31:0] reg16_out,
  output [31:0] reg17_out,
  output [31:0] reg18_out,
  output [31:0] reg19_out,
  output [31:0] reg20_out,
  output [31:0] reg21_out,
  output [31:0] reg22_out,
  output [31:0] reg23_out,
  output [31:0] reg24_out,
  output [31:0] reg25_out,
  output [31:0] reg26_out,
  output [31:0] reg27_out,
  output [31:0] reg28_out,
  output [31:0] reg29_out,
  output [31:0] reg30_out,
  output [31:0] reg31_out
);

  \reg  reg_1 (.D(write_data), .reg_on_off(reg01_on_off), .Q(reg01_out));
  \reg  reg_2 (.D(write_data), .reg_on_off(reg02_on_off), .Q(reg02_out));
  \reg  reg_3 (.D(write_data), .reg_on_off(reg03_on_off), .Q(reg03_out));
  \reg  reg_4 (.D(write_data), .reg_on_off(reg04_on_off), .Q(reg04_out));
  \reg  reg_5 (.D(write_data), .reg_on_off(reg05_on_off), .Q(reg05_out));
  \reg  reg_6 (.D(write_data), .reg_on_off(reg06_on_off), .Q(reg06_out));
  \reg  reg_7 (.D(write_data), .reg_on_off(reg07_on_off), .Q(reg07_out));
  \reg  reg_8 (.D(write_data), .reg_on_off(reg08_on_off), .Q(reg08_out));
  \reg  reg_9 (.D(write_data), .reg_on_off(reg09_on_off), .Q(reg09_out));
  \reg  reg_10 (.D(write_data), .reg_on_off(reg10_on_off), .Q(reg10_out));
  \reg  reg_11 (.D(write_data), .reg_on_off(reg11_on_off), .Q(reg11_out));
  \reg  reg_12 (.D(write_data), .reg_on_off(reg12_on_off), .Q(reg12_out));
  \reg  reg_13 (.D(write_data), .reg_on_off(reg13_on_off), .Q(reg13_out));
  \reg  reg_14 (.D(write_data), .reg_on_off(reg14_on_off), .Q(reg14_out));
  \reg  reg_15 (.D(write_data), .reg_on_off(reg15_on_off), .Q(reg15_out));
  \reg  reg_16 (.D(write_data), .reg_on_off(reg16_on_off), .Q(reg16_out));
  \reg  reg_17 (.D(write_data), .reg_on_off(reg17_on_off), .Q(reg17_out));
  \reg  reg_18 (.D(write_data), .reg_on_off(reg18_on_off), .Q(reg18_out));
  \reg  reg_19 (.D(write_data), .reg_on_off(reg19_on_off), .Q(reg19_out));
  \reg  reg_20 (.D(write_data), .reg_on_off(reg20_on_off), .Q(reg20_out));
  \reg  reg_21 (.D(write_data), .reg_on_off(reg21_on_off), .Q(reg21_out));
  \reg  reg_22 (.D(write_data), .reg_on_off(reg22_on_off), .Q(reg22_out));
  \reg  reg_23 (.D(write_data), .reg_on_off(reg23_on_off), .Q(reg23_out));
  \reg  reg_24 (.D(write_data), .reg_on_off(reg24_on_off), .Q(reg24_out));
  \reg  reg_25 (.D(write_data), .reg_on_off(reg25_on_off), .Q(reg25_out));
  \reg  reg_26 (.D(write_data), .reg_on_off(reg26_on_off), .Q(reg26_out));
  \reg  reg_27 (.D(write_data), .reg_on_off(reg27_on_off), .Q(reg27_out));
  \reg  reg_28 (.D(write_data), .reg_on_off(reg28_on_off), .Q(reg28_out));
  \reg  reg_29 (.D(write_data), .reg_on_off(reg29_on_off), .Q(reg29_out));
  \reg  reg_30 (.D(write_data), .reg_on_off(reg30_on_off), .Q(reg30_out));
  \reg  reg_31 (.D(write_data), .reg_on_off(reg31_on_off), .Q(reg31_out));
endmodule

module regfile (
  input  [4:0] write_register,
  input  [31:0] Data,
  input  write_enable,
  input  [4:0] read_register,
  output [31:0] s0_Value,
  output [31:0] s1_Value,
  output [31:0] s2_Value,
  output [31:0] ra_Value,
  output [31:0] sp_Value,
  output [31:0] read_data,
  output [31:0] reg_1_val,
  output [31:0] reg_2_val,
  output [31:0] reg_3_val
);

  wire clk, demultiplexer_1_out1, demultiplexer_1_out2, demultiplexer_1_out3, demultiplexer_1_out4,
       demultiplexer_1_out5, demultiplexer_1_out6, demultiplexer_1_out7, demultiplexer_1_out8,
       demultiplexer_1_out9, demultiplexer_1_out10, demultiplexer_1_out11, demultiplexer_1_out12,
       demultiplexer_1_out13, demultiplexer_1_out14, demultiplexer_1_out15, demultiplexer_1_out16,
       demultiplexer_1_out17, demultiplexer_1_out18, demultiplexer_1_out19, demultiplexer_1_out20,
       demultiplexer_1_out21, demultiplexer_1_out22, demultiplexer_1_out23, demultiplexer_1_out24,
       demultiplexer_1_out25, demultiplexer_1_out26, demultiplexer_1_out27, demultiplexer_1_out28,
       demultiplexer_1_out29, demultiplexer_1_out30, demultiplexer_1_out31;
  wire [31:0] reg04_out, reg05_out, reg06_out, reg07_out, reg08_out, reg09_out, reg10_out, reg11_out,
       reg12_out, reg13_out, reg14_out, reg15_out, reg19_out, reg20_out, reg21_out, reg22_out, reg23_out,
       reg24_out, reg25_out, reg26_out, reg27_out, reg28_out, reg30_out;

  Clock clock_1 (.out(clk));
  Demultiplexer #(.select(5), .enable("false")) demultiplexer_1 (
    .out1(demultiplexer_1_out1), .out2(demultiplexer_1_out2), .out3(demultiplexer_1_out3),
    .out4(demultiplexer_1_out4), .out5(demultiplexer_1_out5), .out6(demultiplexer_1_out6),
    .out7(demultiplexer_1_out7), .out8(demultiplexer_1_out8), .out9(demultiplexer_1_out9),
    .out10(demultiplexer_1_out10), .out11(demultiplexer_1_out11), .out12(demultiplexer_1_out12),
    .out13(demultiplexer_1_out13), .out14(demultiplexer_1_out14), .out15(demultiplexer_1_out15),
    .out16(demultiplexer_1_out16), .out17(demultiplexer_1_out17), .out18(demultiplexer_1_out18),
    .out19(demultiplexer_1_out19), .out20(demultiplexer_1_out20), .out21(demultiplexer_1_out21),
    .out22(demultiplexer_1_out22), .out23(demultiplexer_1_out23), .out24(demultiplexer_1_out24),
    .out25(demultiplexer_1_out25), .out26(demultiplexer_1_out26), .out27(demultiplexer_1_out27),
    .out28(demultiplexer_1_out28), .out29(demultiplexer_1_out29), .out30(demultiplexer_1_out30),
    .out31(demultiplexer_1_out31), .in(write_enable), .sel(write_register));  // open: out0
  regs regs_1 (
    .write_data(Data), .reg01_on_off(demultiplexer_1_out1), .reg02_on_off(demultiplexer_1_out2),
    .reg03_on_off(demultiplexer_1_out3), .reg04_on_off(demultiplexer_1_out4),
    .reg05_on_off(demultiplexer_1_out5), .reg06_on_off(demultiplexer_1_out6),
    .reg07_on_off(demultiplexer_1_out7), .reg08_on_off(demultiplexer_1_out8),
    .reg09_on_off(demultiplexer_1_out9), .reg10_on_off(demultiplexer_1_out10),
    .reg11_on_off(demultiplexer_1_out11), .reg12_on_off(demultiplexer_1_out12),
    .reg13_on_off(demultiplexer_1_out13), .reg14_on_off(demultiplexer_1_out14),
    .reg15_on_off(demultiplexer_1_out15), .reg16_on_off(demultiplexer_1_out16),
    .reg17_on_off(demultiplexer_1_out17), .reg18_on_off(demultiplexer_1_out18),
    .reg19_on_off(demultiplexer_1_out19), .reg20_on_off(demultiplexer_1_out20),
    .reg21_on_off(demultiplexer_1_out21), .reg22_on_off(demultiplexer_1_out22),
    .reg23_on_off(demultiplexer_1_out23), .reg24_on_off(demultiplexer_1_out24),
    .reg25_on_off(demultiplexer_1_out25), .reg26_on_off(demultiplexer_1_out26),
    .reg27_on_off(demultiplexer_1_out27), .reg28_on_off(demultiplexer_1_out28),
    .reg29_on_off(demultiplexer_1_out29), .reg30_on_off(demultiplexer_1_out30),
    .reg31_on_off(demultiplexer_1_out31), .reg01_out(reg_1_val), .reg02_out(reg_2_val),
    .reg03_out(reg_3_val), .reg04_out(reg04_out), .reg05_out(reg05_out), .reg06_out(reg06_out),
    .reg07_out(reg07_out), .reg08_out(reg08_out), .reg09_out(reg09_out), .reg10_out(reg10_out),
    .reg11_out(reg11_out), .reg12_out(reg12_out), .reg13_out(reg13_out), .reg14_out(reg14_out),
    .reg15_out(reg15_out), .reg16_out(s0_Value), .reg17_out(s1_Value), .reg18_out(s2_Value),
    .reg19_out(reg19_out), .reg20_out(reg20_out), .reg21_out(reg21_out), .reg22_out(reg22_out),
    .reg23_out(reg23_out), .reg24_out(reg24_out), .reg25_out(reg25_out), .reg26_out(reg26_out),
    .reg27_out(reg27_out), .reg28_out(reg28_out), .reg29_out(sp_Value), .reg30_out(reg30_out),
    .reg31_out(ra_Value));
  Multiplexer #(.select(5), .width(32), .enable("false")) multiplexer_1 (
    .in1(reg_1_val), .in2(reg_2_val), .in3(reg_3_val), .in4(reg04_out), .in5(reg05_out), .in6(reg06_out),
    .in7(reg07_out), .in8(reg08_out), .in9(reg09_out), .in10(reg10_out), .in11(reg11_out), .in12(reg12_out),
    .in13(reg13_out), .in14(reg14_out), .in15(reg15_out), .in16(s0_Value), .in17(s1_Value), .in18(s2_Value),
    .in19(reg19_out), .in20(reg20_out), .in21(reg21_out), .in22(reg22_out), .in23(reg23_out),
    .in24(reg24_out), .in25(reg25_out), .in26(reg26_out), .in27(reg27_out), .in28(reg28_out),
    .in29(sp_Value), .in30(reg30_out), .in31(ra_Value), .out(read_data), .sel(read_register));  // open: in0

  // Other names for the same wires on the sheet: read_reg[4:0] = read_register; reg01_out[31:0] = reg_1_val;
  //   reg02_out[31:0] = reg_2_val; reg03_out[31:0] = reg_3_val; reg16_out[31:0] = s0_Value;
  //   reg17_out[31:0] = s1_Value; reg18_out[31:0] = s2_Value; reg29_out[31:0] = sp_Value; reg31_out[31:0] = ra_Value;
  //   write_data[31:0] = Data; write_en = write_enable; write_reg[4:0] = write_register

  // Notes on the sheet:
  //   Debug
  //   Write
  //   Read
endmodule
