// Logisim project 302_RAM.circ as structural Verilog: 2 circuits, main circuit main
module main (
  input  [7:0] Store_Data,
  input  in_2,
  input  [7:0] Address,
  input  [1:0] Address_2,
  input  read_nwrite,
  input  [7:0] data_write,
  input  selectively_drive_bus,
  output [7:0] out_8,
  output [7:0] data_read
);

  wire and_1_out, and_2_out, and_3_out, and_4_out, and_5_out, and_6_out, and_7_out, and_8_out, clock_1_out,
       clock_2_out, clock_3_out, clock_4_out, clock_5_out, decoder_1_out0, decoder_1_out1, decoder_1_out2,
       decoder_1_out3, not_1_out;
  wire [7:0] register_1_q, register_2_q, register_3_q, register_4_q;

  Clock clock_1 (.out(clock_1_out));
  assign out_8 = in_2 ? Store_Data : 8'bz;  // Controlled_Buffer controlled_buffer_1
  Decoder #(.select(2)) decoder_1 (
    .out0(decoder_1_out0), .out1(decoder_1_out1), .out2(decoder_1_out2), .out3(decoder_1_out3),
    .sel(Address_2), .en(1'b1));
  not not_1 (not_1_out, in_2);
  and and_1 (and_1_out, ~read_nwrite, decoder_1_out0);  // AND_Gate
  and and_2 (and_2_out, decoder_1_out0, read_nwrite);
  and and_3 (and_3_out, ~read_nwrite, decoder_1_out1);  // AND_Gate
  and and_4 (and_4_out, decoder_1_out1, read_nwrite);
  and and_5 (and_5_out, ~read_nwrite, decoder_1_out2);  // AND_Gate
  and and_6 (and_6_out, decoder_1_out2, read_nwrite);
  and and_7 (and_7_out, ~read_nwrite, decoder_1_out3);  // AND_Gate
  and and_8 (and_8_out, decoder_1_out3, read_nwrite);
  RAM ram_1 (.addr(Address), .data(out_8), .clk(clock_1_out), .ld(not_1_out));  // open: sel, clr
  Register register_1 (.D(data_read), .en(and_1_out), .Q(register_1_q), .clk(clock_2_out));  // open: clr
  Clock clock_2 (.out(clock_2_out));
  Register register_2 (.D(data_read), .en(and_3_out), .Q(register_2_q), .clk(clock_3_out));  // open: clr
  Clock clock_3 (.out(clock_3_out));
  Register register_3 (.D(data_read), .en(and_5_out), .Q(register_3_q), .clk(clock_4_out));  // open: clr
  Clock clock_4 (.out(clock_4_out));
  Register register_4 (.D(data_read), .en(and_7_out), .Q(register_4_q), .clk(clock_5_out));  // open: clr
  Clock clock_5 (.out(clock_5_out));
  assign data_read = and_2_out ? register_1_q : 8'bz;  // Controlled_Buffer controlled_buffer_2
  assign data_read = and_4_out ? register_2_q : 8'bz;  // Controlled_Buffer controlled_buffer_3
  assign data_read = and_6_out ? register_3_q : 8'bz;  // Controlled_Buffer controlled_buffer_4
  assign data_read = and_8_out ? register_4_q : 8'bz;  // Controlled_Buffer controlled_buffer_5
  assign data_read = selectively_drive_bus ? data_write : 8'bz;  // Controlled_Buffer controlled_buffer_6

  // Notes on the sheet:
  //   0 => Write-Mode
  //   1 => data_write passes through
endmodule

module memory_cell (
  input  select,
  input  clk,
  input  read_nwrite,
  output [7:0] stored_value,
  output [7:0] data
);

  wire and_1_out, and_2_out;

  and and_1 (and_1_out, ~read_nwrite, select);  // AND_Gate
  and and_2 (and_2_out, select, read_nwrite);
  Register register_1 (.D(data), .en(and_1_out), .Q(stored_value), .clk(clk));  // open: clr
  assign data = and_2_out ? stored_value : 8'bz;  // Controlled_Buffer controlled_buffer_1
endmodule
