// Logisim project 400_Data-Path.circ as structural Verilog: 1 circuit, main circuit main
module main (
  input  in_1,
  input  Toggle_Selector,
  input  in_3
);

  wire d_ff_1_qn, multiplexer_1_out;

  Multiplexer #(.enable("false")) multiplexer_1 (
    .in0(in_1), .in1(d_ff_1_qn), .out(multiplexer_1_out), .sel(Toggle_Selector));
  D_Flip_Flop d_ff_1 (.clk(in_3), .D(multiplexer_1_out), .Qn(d_ff_1_qn), .en(1'b1));  // open: Q, preset, reset
endmodule
