// Logisim project Adder.circ as structural Verilog: 1 circuit, main circuit Adder
module Adder (
  input  [31:0] in_1,
  input  [31:0] in_2,
  output [31:0] out_3
);

  Adder_part #(.width(32)) adder_1 (.a(in_1), .b(in_2), .out(out_3));  // open: cin, cout
endmodule
