// Logisim project CPU.circ as structural Verilog: 9 circuits, main circuit main
module main (
  input  in_1,
  input  in_2,
  input  in_3,
  output Signed_OverFlow,
  output equal
);

  wire undriven;
  wire [4:0] instruction_memory_1_instr_15_11, instruction_memory_1_instr_20_16,
       instruction_memory_1_instr_25_21, mux_reg_file_1_zero_or_one;
  wire [5:0] instruction_memory_1_instr_5_0;
  wire [15:0] instruction_memory_1_instr_15_0;
  wire [23:0] data_memory_1_address_2, memory_data_temp_1_address;
  wire [31:0] adder_1_out_3, alu_1_result, data_memory_1_read_data, four_1_four, program_counter_1_pc, ra,
       register_file_1_ra, register_file_1_read_data_1, register_file_1_read_data_2, register_file_1_s0,
       register_file_1_s1, register_file_1_s2, register_file_1_sp, s0, s1, s2, sign_extend_1_out_2, sp,
       write_data;

  // Probe on s0
  four four_1 (.four(four_1_four));
  program_counter program_counter_1 (.PC(program_counter_1_pc));
  // Probe on program_counter_1_pc
  // Probe on s1
  Adder adder_1 (.in_1(program_counter_1_pc), .in_2(four_1_four), .out_3(adder_1_out_3));
  // Probe on s2
  Instruction_Memory instruction_memory_1 (
    .Read_Address(program_counter_1_pc), .Instr_25_21(instruction_memory_1_instr_25_21),
    .Instr_20_16(instruction_memory_1_instr_20_16), .Instr_15_11(instruction_memory_1_instr_15_11),
    .Instr_15_0(instruction_memory_1_instr_15_0), .Instr_5_0(instruction_memory_1_instr_5_0));
  // Probe on ra
  // Probe on instruction_memory_1_instr_25_21
  // Probe on sp
  // Probe on instruction_memory_1_instr_20_16
  // Probe on instruction_memory_1_instr_15_0
  Debug debug_1 (
    .s0_out(s0), .s1_out(s1), .s2_out(s2), .ra_out(ra), .sp_out(sp), .s0(register_file_1_s0),
    .s1(register_file_1_s1), .s2(register_file_1_s2), .ra(register_file_1_ra), .sp(register_file_1_sp));
  MUX_Reg_File mux_reg_file_1 (
    .Zero(instruction_memory_1_instr_20_16), .One(instruction_memory_1_instr_15_11),
    .Zero_or_One(mux_reg_file_1_zero_or_one), .Control(in_3));
  Sign_Extend sign_extend_1 (.in_1(instruction_memory_1_instr_15_0), .out_2(sign_extend_1_out_2));
  // Probe on write_data
  Register_File register_file_1 (
    .Read_Register_1(instruction_memory_1_instr_25_21), .Read_Register_2(instruction_memory_1_instr_20_16),
    .Write_Register(mux_reg_file_1_zero_or_one), .Read_Data_1(register_file_1_read_data_1),
    .Read_Data_2(register_file_1_read_data_2), .s0(register_file_1_s0), .s1(register_file_1_s1),
    .s2(register_file_1_s2), .ra(register_file_1_ra), .sp(register_file_1_sp), .Write_Data(write_data),
    .RegWrite(1'b1), .clk(in_2));
  // Probe on undriven
  // Probe on register_file_1_read_data_1
  // Probe on sign_extend_1_out_2
  alu alu_1 (
    .Switch(4'b0101), .X(register_file_1_read_data_1), .Equal(equal), .Result(alu_1_result),
    .Signed_Overflow_18670403(Signed_OverFlow), .Y(sign_extend_1_out_2));
  // Probe on register_file_1_read_data_2
  // Probe on alu_1_result
  // Probe on data_memory_1_address_2
  // Probe on memory_data_temp_1_address
  Data_Memory data_memory_1 (
    .Address(alu_1_result), .in_2(in_2), .in_3(in_1), .Write_Data(register_file_1_read_data_2),
    .Read_Data(data_memory_1_read_data), .address_2(data_memory_1_address_2));
  // Probe on data_memory_1_read_data
  memory_data_temp memory_data_temp_1 (
    .instruction(write_data), .fetch_addr(alu_1_result), .address(memory_data_temp_1_address));
  // Probe on write_data

  // Other names for the same wires on the sheet: clk = in_2; MemWr = in_1; RegDst = in_3

  // Notes on the sheet:
  //   rs
  //   rt
  //   -> ALU-Control
  //   ALU-Control (5=Add)
  //   Address
  //   Write-Data
  //   Note the extra delay for the Data-Memory
endmodule

module Decode (
  input  [31:0] Instruction,
  output [5:0] opcode,
  output [4:0] RR1,
  output [4:0] RR2,
  output [15:0] out_5,
  output [5:0] func,
  output [4:0] out_7
);


  assign func = Instruction[5:0];
  assign opcode = Instruction[31:26];
  assign out_5 = Instruction[15:0];
  assign out_7 = Instruction[15:11];
  assign RR1 = Instruction[25:21];
  assign RR2 = Instruction[20:16];

  // Notes on the sheet:
  //   [26:31]
  //   [21:25]
  //   [16:20]
  //   [0:15]
  //   [0:5]
  //   [11:15]
endmodule

module Sign_Extend (
  input  [15:0] in_1,
  output [31:0] out_2
);

  assign out_2 = {{16{in_1[15]}}, in_1};  // Bit_Extender bit_extender_1
endmodule

module Instruction_Memory (
  input  [31:0] Read_Address,
  output [4:0] Instr_25_21,
  output [4:0] Instr_20_16,
  output [4:0] Instr_15_11,
  output [15:0] Instr_15_0,
  output [5:0] Instr_5_0
);

  wire [31:0] rom_1_data;

  ROM #(.addrWidth(24), .dataWidth(32)) rom_1 (.addr(Read_Address[25:2]), .data(rom_1_data));
  Decode decode_1 (
    .Instruction(rom_1_data), .RR1(Instr_25_21), .RR2(Instr_20_16), .out_5(Instr_15_0), .func(Instr_5_0),
    .out_7(Instr_15_11));  // open: opcode

  // Notes on the sheet:
  //   contents of rom_1 (hex, n*v repeats v):
  //   0 8d100004 ae530018 8e510018
  //   Instruction Memory
  //   Address Bit-Width = N=24 = 2^24=~16-Million-Addresses
  //   Data Bit-Width = M=32
  //   NxM=24x32=<Address-Bits>x<Data-Bits>
endmodule

module MUX_Reg_File (
  input  [4:0] Zero,
  input  [4:0] One,
  input  Control,
  output [4:0] Zero_or_One
);

  Multiplexer #(.width(5), .enable("false")) multiplexer_1 (.in0(Zero), .in1(One), .out(Zero_or_One), .sel(Control));
endmodule

module four (
  output [31:0] four
);


  assign four = 32'h4;
endmodule

module Debug (
  input  [31:0] s0,
  input  [31:0] s1,
  input  [31:0] s2,
  input  [31:0] ra,
  input  [31:0] sp,
  output [31:0] s0_out,
  output [31:0] s1_out,
  output [31:0] s2_out,
  output [31:0] ra_out,
  output [31:0] sp_out
);


  assign ra_out = ra;
  assign s0_out = s0;
  assign s1_out = s1;
  assign s2_out = s2;
  assign sp_out = sp;
endmodule

module Register_File (
  input  [4:0] Read_Register_1,
  input  [4:0] Read_Register_2,
  input  [4:0] Write_Register,
  input  [31:0] Write_Data,
  input  RegWrite,
  input  clk,
  output [31:0] s0,
  output [31:0] s1,
  output [31:0] s2,
  output [31:0] ra,
  output [31:0] sp,
  output [31:0] Read_Data_1,
  output [31:0] Read_Data_2
);

  wire demultiplexer_1_out1, demultiplexer_1_out2, demultiplexer_1_out3, demultiplexer_1_out4,
       demultiplexer_1_out5, demultiplexer_1_out6, demultiplexer_1_out7, demultiplexer_1_out8,
       demultiplexer_1_out9, demultiplexer_1_out10, demultiplexer_1_out11, demultiplexer_1_out12,
       demultiplexer_1_out13, demultiplexer_1_out14, demultiplexer_1_out15, demultiplexer_1_out16,
       demultiplexer_1_out17, demultiplexer_1_out18, demultiplexer_1_out19, demultiplexer_1_out20,
       demultiplexer_1_out21, demultiplexer_1_out22, demultiplexer_1_out23, demultiplexer_1_out24,
       demultiplexer_1_out25, demultiplexer_1_out26, demultiplexer_1_out27, demultiplexer_1_out28,
       demultiplexer_1_out29, demultiplexer_1_out30, demultiplexer_1_out31, reg00_on_off;
  wire [31:0] reg01_out, reg02_out, reg03_out, reg04_out, reg05_out, reg06_out, reg07_out, reg08_out,
       reg09_out, reg10_out, reg11_out, reg12_out, reg13_out, reg14_out, reg15_out, reg19_out, reg20_out,
       reg21_out, reg22_out, reg23_out, reg24_out, reg26_out, reg27_out, reg28_out, reg29_out, reg30_out;

  Demultiplexer #(.select(5), .enable("false")) demultiplexer_1 (
    .out0(reg00_on_off), .out1(demultiplexer_1_out1), .out2(demultiplexer_1_out2),
    .out3(demultiplexer_1_out3), .out4(demultiplexer_1_out4), .out5(demultiplexer_1_out5),
    .out6(demultiplexer_1_out6), .out7(demultiplexer_1_out7), .out8(demultiplexer_1_out8),
    .out9(demultiplexer_1_out9), .out10(demultiplexer_1_out10), .out11(demultiplexer_1_out11),
    .out12(demultiplexer_1_out12), .out13(demultiplexer_1_out13), .out14(demultiplexer_1_out14),
    .out15(demultiplexer_1_out15), .out16(demultiplexer_1_out16), .out17(demultiplexer_1_out17),
    .out18(demultiplexer_1_out18), .out19(demultiplexer_1_out19), .out20(demultiplexer_1_out20),
    .out21(demultiplexer_1_out21), .out22(demultiplexer_1_out22), .out23(demultiplexer_1_out23),
    .out24(demultiplexer_1_out24), .out25(demultiplexer_1_out25), .out26(demultiplexer_1_out26),
    .out27(demultiplexer_1_out27), .out28(demultiplexer_1_out28), .out29(demultiplexer_1_out29),
    .out30(demultiplexer_1_out30), .out31(demultiplexer_1_out31), .in(RegWrite), .sel(Write_Register));
  \reg  reg_1 (.D(Write_Data), .reg_on_off(demultiplexer_1_out1), .Q(reg01_out), .clk(clk));
  \reg  reg_2 (.D(Write_Data), .reg_on_off(demultiplexer_1_out2), .Q(reg02_out), .clk(clk));
  \reg  reg_3 (.D(Write_Data), .reg_on_off(demultiplexer_1_out3), .Q(reg03_out), .clk(clk));
  \reg  reg_4 (.D(Write_Data), .reg_on_off(demultiplexer_1_out4), .Q(reg04_out), .clk(clk));
  \reg  reg_5 (.D(Write_Data), .reg_on_off(demultiplexer_1_out5), .Q(reg05_out), .clk(clk));
  \reg  reg_6 (.D(Write_Data), .reg_on_off(demultiplexer_1_out6), .Q(reg06_out), .clk(clk));
  \reg  reg_7 (.D(Write_Data), .reg_on_off(demultiplexer_1_out7), .Q(reg07_out), .clk(clk));
  \reg  reg_8 (.D(Write_Data), .reg_on_off(demultiplexer_1_out8), .Q(reg08_out), .clk(clk));
  \reg  reg_9 (.D(Write_Data), .reg_on_off(demultiplexer_1_out9), .Q(reg09_out), .clk(clk));
  \reg  reg_10 (.D(Write_Data), .reg_on_off(demultiplexer_1_out10), .Q(reg10_out), .clk(clk));
  \reg  reg_11 (.D(Write_Data), .reg_on_off(demultiplexer_1_out11), .Q(reg11_out), .clk(clk));
  \reg  reg_12 (.D(Write_Data), .reg_on_off(demultiplexer_1_out12), .Q(reg12_out), .clk(clk));
  \reg  reg_13 (.D(Write_Data), .reg_on_off(demultiplexer_1_out13), .Q(reg13_out), .clk(clk));
  \reg  reg_14 (.D(Write_Data), .reg_on_off(demultiplexer_1_out14), .Q(reg14_out), .clk(clk));
  \reg  reg_15 (.D(Write_Data), .reg_on_off(demultiplexer_1_out15), .Q(reg15_out), .clk(clk));
  \reg  reg_16 (.D(Write_Data), .reg_on_off(demultiplexer_1_out16), .Q(s0), .clk(clk));
  \reg  reg_17 (.D(Write_Data), .reg_on_off(demultiplexer_1_out17), .Q(s1), .clk(clk));
  \reg  reg_18 (.D(Write_Data), .reg_on_off(demultiplexer_1_out18), .Q(s2), .clk(clk));
  \reg  reg_19 (.D(Write_Data), .reg_on_off(demultiplexer_1_out19), .Q(reg19_out), .clk(clk));
  \reg  reg_20 (.D(Write_Data), .reg_on_off(demultiplexer_1_out20), .Q(reg20_out), .clk(clk));
  \reg  reg_21 (.D(Write_Data), .reg_on_off(demultiplexer_1_out21), .Q(reg21_out), .clk(clk));
  \reg  reg_22 (.D(Write_Data), .reg_on_off(demultiplexer_1_out22), .Q(reg22_out), .clk(clk));
  \reg  reg_23 (.D(Write_Data), .reg_on_off(demultiplexer_1_out23), .Q(reg23_out), .clk(clk));
  \reg  reg_24 (.D(Write_Data), .reg_on_off(demultiplexer_1_out24), .Q(reg24_out), .clk(clk));
  \reg  reg_25 (.D(Write_Data), .reg_on_off(demultiplexer_1_out25), .Q(sp), .clk(clk));
  \reg  reg_26 (.D(Write_Data), .reg_on_off(demultiplexer_1_out26), .Q(reg26_out), .clk(clk));
  \reg  reg_27 (.D(Write_Data), .reg_on_off(demultiplexer_1_out27), .Q(reg27_out), .clk(clk));
  \reg  reg_28 (.D(Write_Data), .reg_on_off(demultiplexer_1_out28), .Q(reg28_out), .clk(clk));
  \reg  reg_29 (.D(Write_Data), .reg_on_off(demultiplexer_1_out29), .Q(reg29_out), .clk(clk));
  \reg  reg_30 (.D(Write_Data), .reg_on_off(demultiplexer_1_out30), .Q(reg30_out), .clk(clk));
  \reg  reg_31 (.D(Write_Data), .reg_on_off(demultiplexer_1_out31), .Q(ra), .clk(clk));
  read_mux read_mux_1 (
    .reg01_out(reg01_out), .in_2(reg02_out), .in_3(reg03_out), .in_5(reg04_out), .in_6(reg05_out),
    .in_7(reg06_out), .in_8(reg07_out), .in_9(reg08_out), .in_10(reg09_out), .in_11(reg10_out),
    .in_12(reg11_out), .in_13(reg12_out), .in_14(reg13_out), .in_15(reg14_out), .in_16(reg15_out),
    .in_17(s0), .in_19(s1), .in_20(s2), .in_21(reg19_out), .in_22(reg20_out), .in_23(reg21_out),
    .in_24(reg22_out), .in_25(reg23_out), .in_26(reg24_out), .in_27(sp), .in_28(reg26_out),
    .in_29(reg27_out), .in_30(reg28_out), .in_31(reg29_out), .in_32(reg30_out), .in_33(ra),
    .read_data1(Read_Data_1), .read_reg1(Read_Register_1), .read_data2(Read_Data_2),
    .read_reg2(Read_Register_2));

  // Other names for the same wires on the sheet: R1[31:0] = Read_Data_1; R2[31:0] = Read_Data_2;
  //   read_reg1[4:0] = Read_Register_1; RR1[4:0] = Read_Register_1; read_reg2[4:0] = Read_Register_2;
  //   RR2[4:0] = Read_Register_2; reg16_out[31:0] = s0; reg17_out[31:0] = s1; reg18_out[31:0] = s2;
  //   reg25_out[31:0] = sp; reg31_out[31:0] = ra; WA[31:0] = Write_Data; WE = RegWrite; write_en = RegWrite;
  //   RW[4:0] = Write_Register; write_reg[4:0] = Write_Register

  // Notes on the sheet:
  //   RR1
  //   RR2
  //   RW
  //   WA
  //   WE
  //   ^
  //   Write
  //   $s0 Val
  //   Debug
  //   $s1 Val
  //   $s2 Val
  //   $ra Val
  //   $sp Val
  //   Read
  //   R1
  //   R2
endmodule

module Data_Memory (
  input  [31:0] Address,
  input  in_2,
  input  in_3,
  input  [31:0] Write_Data,
  output [23:0] address_2,
  output [31:0] Read_Data
);

  RAM #(.addrWidth(24), .dataWidth(32), .databus("bibus")) ram_1 (
    .addr(Address[25:2]), .we(in_3), .oe(1'b1), .clk(in_2), .din(Write_Data), .dout(Read_Data));

  assign address_2 = Address[25:2];

  // Other names for the same wires on the sheet: clk = in_2; Write_En = in_3

  // Notes on the sheet:
  //   Data Memory
  //   Address Bit-Width = N=24 = 2^24=~16-Million-Addresses
  //   Data Bit-Width = M=32
  //   NxM=24x32=<Address-Bits>x<Data-Bits>
endmodule
