// Logisim project alu.circ as structural Verilog: 1 circuit, main circuit alu
module alu (
  input  [31:0] X,
  input  [31:0] Y,
  input  [3:0] Switch,
  output Signed_Overflow_18670403,
  output Equal,
  output [31:0] Result
);

  wire and_2_out, and_3_out, and_4_out, and_5_out, and_6_out, and_7_out, and_8_out, and_9_out,
       bitselector_1_out, bitselector_2_out, bitselector_3_out, bitselector_4_out, bitselector_5_out,
       bitselector_6_out, not_1_out, not_2_out, not_3_out, not_4_out, not_5_out, not_6_out, or_2_out,
       or_4_out;
  wire [0:0] slt, sltu;
  wire [31:0] add, addu, \and , \or , sll, sra, srl, sub, subu;

  Shifter #(.width(32)) shifter_1 (.in(Y), .\dist (X[4:0]), .out(sll));
  Shifter #(.width(32), .shift("lr")) shifter_2 (.in(Y), .\dist (X[4:0]), .out(srl));
  Shifter #(.width(32), .shift("ar")) shifter_3 (.in(Y), .\dist (X[4:0]), .out(sra));
  Adder #(.width(32)) adder_1 (.a(X), .b(Y), .out(add));  // open: cin, cout
  BitSelector #(.width(32)) bitselector_1 (.in(X), .out(bitselector_1_out), .sel({5{1'b1}}));
  BitSelector #(.width(32)) bitselector_2 (.in(Y), .out(bitselector_2_out), .sel({5{1'b1}}));
  Adder #(.width(32)) adder_2 (.a(X), .b(Y), .out(addu));  // open: cin, cout
  Subtractor #(.width(32)) subtractor_1 (.a(X), .b(Y), .out(sub));  // open: bin, bout
  BitSelector #(.width(32)) bitselector_3 (.in(X), .out(bitselector_3_out), .sel({5{1'b1}}));
  BitSelector #(.width(32)) bitselector_4 (.in(Y), .out(bitselector_4_out), .sel({5{1'b1}}));
  Subtractor #(.width(32)) subtractor_2 (.a(X), .b(Y), .out(subu));  // open: bin, bout
  assign \and  = X & Y;  // AND_Gate and_1, 32 bits wide
  assign \or  = X | Y;  // OR_Gate or_1, 32 bits wide
  Comparator #(.width(32)) comparator_1 (.a(X), .b(Y), .eq(Equal), .lt(slt[0]));  // open: gt
  Comparator #(.width(32), .mode("unsigned")) comparator_2 (.a(X), .b(Y), .eq(Equal), .lt(sltu[0]));  // open: gt
  BitSelector #(.width(32)) bitselector_5 (.in(add), .out(bitselector_5_out), .sel({5{1'b1}}));
  not not_1 (not_1_out, bitselector_5_out);
  not not_2 (not_2_out, bitselector_1_out);
  and and_2 (and_2_out, not_2_out, not_3_out);
  and and_3 (and_3_out, bitselector_1_out, bitselector_2_out);
  not not_3 (not_3_out, bitselector_2_out);
  BitSelector #(.width(32)) bitselector_6 (.in(sub), .out(bitselector_6_out), .sel({5{1'b1}}));
  not not_4 (not_4_out, bitselector_6_out);
  not not_5 (not_5_out, bitselector_3_out);
  and and_4 (and_4_out, not_5_out, bitselector_4_out);
  and and_5 (and_5_out, bitselector_3_out, not_6_out);
  not not_6 (not_6_out, bitselector_4_out);
  and and_6 (and_6_out, bitselector_5_out, and_2_out);
  and and_7 (and_7_out, not_1_out, and_3_out);
  and and_8 (and_8_out, bitselector_6_out, and_4_out);
  and and_9 (and_9_out, not_4_out, and_5_out);
  or or_2 (or_2_out, and_6_out, and_7_out);
  or or_3 (Signed_Overflow_18670403, or_2_out, or_4_out);
  or or_4 (or_4_out, and_8_out, and_9_out);
  Multiplexer #(.select(4), .width(32)) multiplexer_1 (
    .in0(sll), .in1(srl), .in2(sra), .in5(add), .in6(addu), .in7(sub), .in8(subu), .in9(\and ), .in10(\or ),
    .in11({{31{1'b0}}, slt[0]}), .in12({{31{1'b0}}, sltu[0]}), .out(Result), .sel(Switch));  // open: in3, in4, in13, in14, in15, en

  // Other names for the same wires on the sheet: overflow = Signed_Overflow_18670403; S[3:0] = Switch

  // Notes on the sheet:
  //   INPUTS to your circuit
  //   DON'T CHANGE THE LOCATIONS OF THE INPUTS AND OUTPUTS!
  //   OUTPUTS from your circuit
endmodule
