// Logisim project instruction_memory.circ as structural Verilog: 2 circuits, main circuit main
module main (
  output [31:0] requested_address,
  output [31:0] requested_instruction
);

  wire [23:0] undriven;

  // Probe on requested_address
  bits_2_to_25 bits_2_to_25_1 (.fetch_address(requested_address), .address(undriven));
  ROM #(.addrWidth(24), .dataWidth(32)) rom_1 (.addr(undriven), .data(requested_instruction));
  // Probe on requested_instruction

  // Other names for the same wires on the sheet: fetch_addr[31:0] = requested_address;
  //   instruction[31:0] = requested_instruction

  // Notes on the sheet:
  //   address
endmodule

module bits_2_to_25 (
  input  [23:0] address,
  input  [31:0] fetch_address
);


  assign fetch_address[25:2] = address;

  // Notes on the sheet:
  //   32-bits -> 24-bits
endmodule
