// Logisim project reg_8bit.circ as structural Verilog: 1 circuit, main circuit reg_8
module reg_8 (
  input  [7:0] D,
  input  reg_on_off,
  input  clk,
  output [7:0] Q
);

  Register \reg  (.D(D), .en(reg_on_off), .clk(clk), .Q(Q));  // open: clr
endmodule
