// Logisim project memory_data.circ as structural Verilog: 2 circuits, main circuit memory_data
module memory_data (
  input  [31:0] Address,
  input  in_2,
  input  in_3,
  input  [31:0] Write_Data,
  output [23:0] address_2,
  output [31:0] Read_Data
);

  bits_2_to_25 bits_2_to_25_1 (.fetch_address(Address), .out_2(address_2));
  RAM #(.addrWidth(24), .dataWidth(32), .databus("bibus")) ram_1 (
    .addr(address_2), .we(in_3), .oe(1'b1), .clk(in_2), .din(Write_Data), .dout(Read_Data));

  // Other names for the same wires on the sheet: clk = in_2; Write_En = in_3

  // Notes on the sheet:
  //   Address Bit-Width = N=24 = 2^24=~16-Million-Addresses
  //   Data Bit-Width = M=32
  //   NxM=24x32=<Address-Bits>x<Data-Bits>
endmodule

module bits_2_to_25 (
  input  [31:0] fetch_address,
  output [23:0] out_2
);


  assign out_2 = fetch_address[25:2];

  // Notes on the sheet:
  //   32-bits -> 24-bits
endmodule
