// Logisim project memory_instruction.circ as structural Verilog: 2 circuits, main circuit instruction_memory
module instruction_memory (
  input  [31:0] fetch_addr,
  output [31:0] instruction
);

  wire [23:0] bits_2_to_25_1_out_2;

  // Probe on fetch_addr
  bits_2_to_25 bits_2_to_25_1 (.fetch_address(fetch_addr), .out_2(bits_2_to_25_1_out_2));
  ROM #(.addrWidth(24), .dataWidth(32)) rom_1 (.addr(bits_2_to_25_1_out_2), .data(instruction));
  // Probe on instruction

  // Notes on the sheet:
  //   contents of rom_1 (hex, n*v repeats v):
  //   0 8e300004 8e300008 8e30000c 8e300010 8e300014
  //   Address Bit-Width = N=24 = 2^24=~16-Million-Addresses
  //   Data Bit-Width = M=32
  //   NxM=24x32=<Address-Bits>x<Data-Bits>
endmodule

module bits_2_to_25 (
  input  [31:0] fetch_address,
  output [23:0] out_2
);


  assign out_2 = fetch_address[25:2];

  // Notes on the sheet:
  //   32-bits -> 24-bits
endmodule
