// Logisim project program_counter.circ as structural Verilog: 2 circuits, main circuit program_counter
module program_counter (
  output [31:0] PC
);

  wire clock_1_out;
  wire [31:0] adder_1_out_3;

  Adder adder_1 (.in_1(PC), .in_2(32'h4), .out_3(adder_1_out_3));
  // Probe on adder_1_out_3
  reg32 reg32_1 (.D(adder_1_out_3), .reg_on_off(1'b1), .Q(PC), .clk(clock_1_out));
  Clock clock_1 (.out(clock_1_out));
endmodule

module Adder (
  input  [31:0] in_1,
  input  [31:0] in_2,
  output [31:0] out_3
);

  Adder_part #(.width(32)) adder_1 (.a(in_1), .b(in_2), .out(out_3));  // open: cin, cout
endmodule
