// Logisim project reg_32bit.circ as structural Verilog: 1 circuit, main circuit reg32
module reg32 (
  input  [31:0] D,
  input  reg_on_off,
  input  clk,
  output [31:0] Q
);

  Register #(.width(32)) \reg  (.D(D), .en(reg_on_off), .clk(clk), .Q(Q));  // open: clr
endmodule
