// Logisim project test_harness..circ as structural Verilog: 2 circuits, main circuit main
module main (
  output [7:0] test_number,
  output [31:0] reg_16_val,
  output [31:0] reg_17_val,
  output [31:0] reg_18_val,
  output [31:0] reg_19_val,
  output [31:0] reg_20_val,
  output [31:0] Read_Data_1,
  output [31:0] Read_Data_1_2
);

  wire adder_1_cout, clock_1_out, clock_2_out;
  wire [7:0] adder_1_out;
  wire [15:0] rom_2_data;
  wire [31:0] Write_Data;

  ROM #(.dataWidth(32)) rom_1 (.addr(test_number), .data(Write_Data));
  reg_8 reg_8_1 (.D(adder_1_out), .reg_on_off(1'b1), .clk(clock_1_out), .Q(test_number));
  Clock clock_1 (.out(clock_1_out));
  Adder adder_1 (.a(8'h1), .b(test_number), .out(adder_1_out), .cout(adder_1_cout));  // open: cin
  ROM #(.dataWidth(16)) rom_2 (.addr(test_number), .data(rom_2_data));
  regfile regfile_1 (
    .read_reg1(rom_2_data[4:0]), .read_reg2(rom_2_data[9:5]), .write_register(rom_2_data[14:10]),
    .Data(Write_Data), .write_enable(rom_2_data[15]), .clock(clock_2_out), .read_data1(Read_Data_1),
    .read_data2(Read_Data_1_2), .reg_16_val(reg_16_val), .reg_17_val(reg_17_val), .reg_18_val(reg_18_val),
    .reg_19_val(reg_19_val), .reg_20_val(reg_20_val));
  Clock clock_2 (.out(clock_2_out));

  // Notes on the sheet:
  //   $s0 Val
  //   Debug
  //   $s1 Val
  //   $s2 Val
  //   $ra Val
  //   $sp Val
endmodule

module reg_8 (
  input  [7:0] D,
  input  reg_on_off,
  input  clk,
  output [7:0] Q
);

  Register \reg  (.D(D), .en(reg_on_off), .clk(clk), .Q(Q));  // open: clr
endmodule
