// Logisim project regfile_evolution_w_test_harness.circ as structural Verilog: 7 circuits, main circuit main
module main (
  output [7:0] test_number,
  output [31:0] reg_16_val,
  output [31:0] reg_17_val,
  output [31:0] reg_18_val,
  output [31:0] reg_19_val,
  output [31:0] reg_20_val,
  output [31:0] Read_Data_1,
  output [31:0] Read_Data_1_2
);

  wire adder_1_cout, clock_1_out, clock_2_out;
  wire [7:0] adder_1_out;
  wire [15:0] rom_2_data;
  wire [31:0] Write_Data;

  ROM #(.dataWidth(32)) rom_1 (.addr(test_number), .data(Write_Data));
  reg_8 reg_8_1 (.D(adder_1_out), .reg_on_off(1'b1), .clk(clock_1_out), .Q(test_number));
  Clock clock_1 (.out(clock_1_out));
  Adder adder_1 (.a(8'h1), .b(test_number), .out(adder_1_out), .cout(adder_1_cout));  // open: cin
  ROM #(.dataWidth(16)) rom_2 (.addr(test_number), .data(rom_2_data));
  regfile regfile_1 (
    .read_reg1(rom_2_data[4:0]), .read_reg2(rom_2_data[9:5]), .write_register(rom_2_data[14:10]),
    .Data(Write_Data), .write_enable(rom_2_data[15]), .clock(clock_2_out), .read_data1(Read_Data_1),
    .read_data2(Read_Data_1_2), .reg_16_val(reg_16_val), .reg_17_val(reg_17_val), .reg_18_val(reg_18_val),
    .reg_19_val(reg_19_val), .reg_20_val(reg_20_val));
  Clock clock_2 (.out(clock_2_out));

  // Notes on the sheet:
  //   $s0 Val
  //   Debug
  //   $s1 Val
  //   $s2 Val
  //   $ra Val
  //   $sp Val
endmodule

module \reg  (
  input  [31:0] D,
  input  reg_on_off,
  input  clk,
  output [31:0] Q
);

  Register #(.width(32)) \reg  (.D(D), .en(reg_on_off), .clk(clk), .Q(Q));  // open: clr
endmodule

module regs (
  input  in_1,
  input  reg01_on_off,
  input  reg02_on_off,
  input  reg03_on_off,
  input  reg04_on_off,
  input  reg05_on_off,
  input  reg06_on_off,
  input  reg07_on_off,
  input  reg08_on_off,
  input  reg09_on_off,
  input  reg10_on_off,
  input  reg11_on_off,
  input  reg12_on_off,
  input  reg13_on_off,
  input  reg14_on_off,
  input  reg15_on_off,
  input  reg16_on_off,
  input  reg17_on_off,
  input  reg18_on_off,
  input  reg19_on_off,
  input  reg20_on_off,
  input  reg21_on_off,
  input  reg22_on_off,
  input  reg23_on_off,
  input  reg24_on_off,
  input  reg25_on_off,
  input  reg26_on_off,
  input  reg27_on_off,
  input  reg28_on_off,
  input  reg29_on_off,
  input  reg30_on_off,
  input  reg31_on_off,
  input  [31:0] write_data,
  output [31:0] reg01_out,
  output [31:0] reg02_out,
  output [31:0] reg03_out,
  output [31:0] reg04_out,
  output [31:0] reg05_out,
  output [31:0] reg06_out,
  output [31:0] reg07_out,
  output [31:0] reg08_out,
  output [31:0] reg09_out,
  output [31:0] reg10_out,
  output [31:0] reg11_out,
  output [31:0] reg12_out,
  output [31:0] reg13_out,
  output [31:0] reg14_out,
  output [31:0] reg15_out,
  output [31:0] reg16_out,
  output [31:0] reg17_out,
  output [31:0] reg18_out,
  output [31:0] reg19_out,
  output [31:0] reg20_out,
  output [31:0] reg21_out,
  output [31:0] reg22_out,
  output [31:0] reg23_out,
  output [31:0] reg24_out,
  output [31:0] reg25_out,
  output [31:0] reg26_out,
  output [31:0] reg27_out,
  output [31:0] reg28_out,
  output [31:0] reg29_out,
  output [31:0] reg30_out,
  output [31:0] reg31_out
);

  \reg  reg_1 (.D(write_data), .reg_on_off(reg01_on_off), .Q(reg01_out), .clk(in_1));
  \reg  reg_2 (.D(write_data), .reg_on_off(reg02_on_off), .Q(reg02_out), .clk(in_1));
  \reg  reg_3 (.D(write_data), .reg_on_off(reg03_on_off), .Q(reg03_out), .clk(in_1));
  \reg  reg_4 (.D(write_data), .reg_on_off(reg04_on_off), .Q(reg04_out), .clk(in_1));
  \reg  reg_5 (.D(write_data), .reg_on_off(reg05_on_off), .Q(reg05_out), .clk(in_1));
  \reg  reg_6 (.D(write_data), .reg_on_off(reg06_on_off), .Q(reg06_out), .clk(in_1));
  \reg  reg_7 (.D(write_data), .reg_on_off(reg07_on_off), .Q(reg07_out), .clk(in_1));
  \reg  reg_8 (.D(write_data), .reg_on_off(reg08_on_off), .Q(reg08_out), .clk(in_1));
  \reg  reg_9 (.D(write_data), .reg_on_off(reg09_on_off), .Q(reg09_out), .clk(in_1));
  \reg  reg_10 (.D(write_data), .reg_on_off(reg10_on_off), .Q(reg10_out), .clk(in_1));
  \reg  reg_11 (.D(write_data), .reg_on_off(reg11_on_off), .Q(reg11_out), .clk(in_1));
  \reg  reg_12 (.D(write_data), .reg_on_off(reg12_on_off), .Q(reg12_out), .clk(in_1));
  \reg  reg_13 (.D(write_data), .reg_on_off(reg13_on_off), .Q(reg13_out), .clk(in_1));
  \reg  reg_14 (.D(write_data), .reg_on_off(reg14_on_off), .Q(reg14_out), .clk(in_1));
  \reg  reg_15 (.D(write_data), .reg_on_off(reg15_on_off), .Q(reg15_out), .clk(in_1));
  \reg  reg_16 (.D(write_data), .reg_on_off(reg16_on_off), .Q(reg16_out), .clk(in_1));
  \reg  reg_17 (.D(write_data), .reg_on_off(reg17_on_off), .Q(reg17_out), .clk(in_1));
  \reg  reg_18 (.D(write_data), .reg_on_off(reg18_on_off), .Q(reg18_out), .clk(in_1));
  \reg  reg_19 (.D(write_data), .reg_on_off(reg19_on_off), .Q(reg19_out), .clk(in_1));
  \reg  reg_20 (.D(write_data), .reg_on_off(reg20_on_off), .Q(reg20_out), .clk(in_1));
  \reg  reg_21 (.D(write_data), .reg_on_off(reg21_on_off), .Q(reg21_out), .clk(in_1));
  \reg  reg_22 (.D(write_data), .reg_on_off(reg22_on_off), .Q(reg22_out), .clk(in_1));
  \reg  reg_23 (.D(write_data), .reg_on_off(reg23_on_off), .Q(reg23_out), .clk(in_1));
  \reg  reg_24 (.D(write_data), .reg_on_off(reg24_on_off), .Q(reg24_out), .clk(in_1));
  \reg  reg_25 (.D(write_data), .reg_on_off(reg25_on_off), .Q(reg25_out), .clk(in_1));
  \reg  reg_26 (.D(write_data), .reg_on_off(reg26_on_off), .Q(reg26_out), .clk(in_1));
  \reg  reg_27 (.D(write_data), .reg_on_off(reg27_on_off), .Q(reg27_out), .clk(in_1));
  \reg  reg_28 (.D(write_data), .reg_on_off(reg28_on_off), .Q(reg28_out), .clk(in_1));
  \reg  reg_29 (.D(write_data), .reg_on_off(reg29_on_off), .Q(reg29_out), .clk(in_1));
  \reg  reg_30 (.D(write_data), .reg_on_off(reg30_on_off), .Q(reg30_out), .clk(in_1));
  \reg  reg_31 (.D(write_data), .reg_on_off(reg31_on_off), .Q(reg31_out), .clk(in_1));
endmodule

module read_mux (
  input  [31:0] reg01_out,
  input  [31:0] in_2,
  input  [31:0] in_3,
  input  [4:0] read_reg1,
  input  [31:0] in_5,
  input  [31:0] in_6,
  input  [31:0] in_7,
  input  [31:0] in_8,
  input  [31:0] in_9,
  input  [31:0] in_10,
  input  [31:0] in_11,
  input  [31:0] in_12,
  input  [31:0] in_13,
  input  [31:0] in_14,
  input  [31:0] in_15,
  input  [31:0] in_16,
  input  [31:0] in_17,
  input  [4:0] read_reg2,
  input  [31:0] in_19,
  input  [31:0] in_20,
  input  [31:0] in_21,
  input  [31:0] in_22,
  input  [31:0] in_23,
  input  [31:0] in_24,
  input  [31:0] in_25,
  input  [31:0] in_26,
  input  [31:0] in_27,
  input  [31:0] in_28,
  input  [31:0] in_29,
  input  [31:0] in_30,
  input  [31:0] in_31,
  input  [31:0] in_32,
  input  [31:0] in_33,
  output [31:0] read_data1,
  output [31:0] read_data2
);

  L_32x1_MUX_893dc589 l_32x1_mux_893dc589_1 (
    .reg01_out(reg01_out), .in_2(in_2), .in_3(in_3), .in_4(in_5), .in_5(in_6), .in_6(in_7), .in_7(in_8),
    .in_9(in_9), .in_10(in_10), .in_11(in_11), .in_12(in_12), .in_13(in_13), .in_14(in_14), .in_15(in_15),
    .in_16(in_16), .in_17(in_17), .in_18(in_19), .in_19(in_20), .in_20(in_21), .in_21(in_22), .in_22(in_23),
    .in_23(in_24), .in_24(in_25), .in_25(in_26), .in_26(in_27), .in_27(in_28), .in_28(in_29), .in_29(in_30),
    .in_30(in_31), .in_31(in_32), .in_32(in_33), .read_data(read_data1), .read_reg(read_reg1));
  L_32x1_MUX_893dc589 l_32x1_mux_893dc589_2 (
    .reg01_out(reg01_out), .in_2(in_2), .in_3(in_3), .in_4(in_5), .in_5(in_6), .in_6(in_7), .in_7(in_8),
    .in_9(in_9), .in_10(in_10), .in_11(in_11), .in_12(in_12), .in_13(in_13), .in_14(in_14), .in_15(in_15),
    .in_16(in_16), .in_17(in_17), .in_18(in_19), .in_19(in_20), .in_20(in_21), .in_21(in_22), .in_22(in_23),
    .in_23(in_24), .in_24(in_25), .in_25(in_26), .in_26(in_27), .in_27(in_28), .in_28(in_29), .in_29(in_30),
    .in_30(in_31), .in_31(in_32), .in_32(in_33), .read_data(read_data2), .read_reg(read_reg2));

  // Other names for the same wires on the sheet: reg01[31:0] = reg01_out; reg02[31:0] = in_2; reg03[31:0] = in_3;
  //   reg04[31:0] = in_5; reg05[31:0] = in_6; reg06[31:0] = in_7; reg07[31:0] = in_8; reg08[31:0] = in_9;
  //   reg09[31:0] = in_10; reg10[31:0] = in_11; reg11[31:0] = in_12; reg12[31:0] = in_13; reg13[31:0] = in_14;
  //   reg14[31:0] = in_15; reg15[31:0] = in_16; reg16[31:0] = in_17; reg17[31:0] = in_19; reg18[31:0] = in_20;
  //   reg19[31:0] = in_21; reg20[31:0] = in_22; reg21[31:0] = in_23; reg22[31:0] = in_24; reg23[31:0] = in_25;
  //   reg24[31:0] = in_26; reg25[31:0] = in_27; reg26[31:0] = in_28; reg27[31:0] = in_29; reg28[31:0] = in_30;
  //   reg29[31:0] = in_31; reg30[31:0] = in_32; reg31[31:0] = in_33
endmodule

module L_32x1_MUX_893dc589 (
  input  [31:0] reg01_out,
  input  [31:0] in_2,
  input  [31:0] in_3,
  input  [31:0] in_4,
  input  [31:0] in_5,
  input  [31:0] in_6,
  input  [31:0] in_7,
  input  [4:0] read_reg,
  input  [31:0] in_9,
  input  [31:0] in_10,
  input  [31:0] in_11,
  input  [31:0] in_12,
  input  [31:0] in_13,
  input  [31:0] in_14,
  input  [31:0] in_15,
  input  [31:0] in_16,
  input  [31:0] in_17,
  input  [31:0] in_18,
  input  [31:0] in_19,
  input  [31:0] in_20,
  input  [31:0] in_21,
  input  [31:0] in_22,
  input  [31:0] in_23,
  input  [31:0] in_24,
  input  [31:0] in_25,
  input  [31:0] in_26,
  input  [31:0] in_27,
  input  [31:0] in_28,
  input  [31:0] in_29,
  input  [31:0] in_30,
  input  [31:0] in_31,
  input  [31:0] in_32,
  output [31:0] read_data
);

  wire [31:0] reg00_out_q;

  Register #(.width(32)) reg00_out (.Q(reg00_out_q), .clr(1'b1));  // open: D, en, clk
  Multiplexer #(.select(5), .width(32), .enable("false")) multiplexer_1 (
    .in0(reg00_out_q), .in1(reg01_out), .in2(in_2), .in3(in_3), .in4(in_4), .in5(in_5), .in6(in_6),
    .in7(in_7), .in8(in_9), .in9(in_10), .in10(in_11), .in11(in_12), .in12(in_13), .in13(in_14),
    .in14(in_15), .in15(in_16), .in16(in_17), .in17(in_18), .in18(in_19), .in19(in_20), .in20(in_21),
    .in21(in_22), .in22(in_23), .in23(in_24), .in24(in_25), .in25(in_26), .in26(in_27), .in27(in_28),
    .in28(in_29), .in29(in_30), .in30(in_31), .in31(in_32), .out(read_data), .sel(read_reg));
endmodule

module regfile (
  input  [4:0] read_reg1,
  input  [4:0] read_reg2,
  input  [4:0] write_register,
  input  [31:0] Data,
  input  write_enable,
  input  clock,
  output [31:0] reg_16_val,
  output [31:0] reg_17_val,
  output [31:0] reg_18_val,
  output [31:0] reg_19_val,
  output [31:0] reg_20_val,
  output [31:0] read_data1,
  output [31:0] read_data2
);

  wire demultiplexer_1_out1, demultiplexer_1_out2, demultiplexer_1_out3, demultiplexer_1_out4,
       demultiplexer_1_out5, demultiplexer_1_out6, demultiplexer_1_out7, demultiplexer_1_out8,
       demultiplexer_1_out9, demultiplexer_1_out10, demultiplexer_1_out11, demultiplexer_1_out12,
       demultiplexer_1_out13, demultiplexer_1_out14, demultiplexer_1_out15, demultiplexer_1_out16,
       demultiplexer_1_out17, demultiplexer_1_out18, demultiplexer_1_out19, demultiplexer_1_out20,
       demultiplexer_1_out21, demultiplexer_1_out22, demultiplexer_1_out23, demultiplexer_1_out24,
       demultiplexer_1_out25, demultiplexer_1_out26, demultiplexer_1_out27, demultiplexer_1_out28,
       demultiplexer_1_out29, demultiplexer_1_out30, demultiplexer_1_out31, reg00_on_off;
  wire [31:0] reg01_out, reg02_out, reg03_out, reg04_out, reg05_out, reg06_out, reg07_out, reg08_out,
       reg09_out, reg10_out, reg11_out, reg12_out, reg13_out, reg14_out, reg15_out, reg19_out, reg20_out,
       reg21_out, reg22_out, reg23_out, reg24_out, reg26_out, reg27_out, reg28_out, reg29_out, reg30_out;

  Demultiplexer #(.select(5), .enable("false")) demultiplexer_1 (
    .out0(reg00_on_off), .out1(demultiplexer_1_out1), .out2(demultiplexer_1_out2),
    .out3(demultiplexer_1_out3), .out4(demultiplexer_1_out4), .out5(demultiplexer_1_out5),
    .out6(demultiplexer_1_out6), .out7(demultiplexer_1_out7), .out8(demultiplexer_1_out8),
    .out9(demultiplexer_1_out9), .out10(demultiplexer_1_out10), .out11(demultiplexer_1_out11),
    .out12(demultiplexer_1_out12), .out13(demultiplexer_1_out13), .out14(demultiplexer_1_out14),
    .out15(demultiplexer_1_out15), .out16(demultiplexer_1_out16), .out17(demultiplexer_1_out17),
    .out18(demultiplexer_1_out18), .out19(demultiplexer_1_out19), .out20(demultiplexer_1_out20),
    .out21(demultiplexer_1_out21), .out22(demultiplexer_1_out22), .out23(demultiplexer_1_out23),
    .out24(demultiplexer_1_out24), .out25(demultiplexer_1_out25), .out26(demultiplexer_1_out26),
    .out27(demultiplexer_1_out27), .out28(demultiplexer_1_out28), .out29(demultiplexer_1_out29),
    .out30(demultiplexer_1_out30), .out31(demultiplexer_1_out31), .in(write_enable), .sel(write_register));
  regs regs_1 (
    .reg01_on_off(demultiplexer_1_out1), .reg02_on_off(demultiplexer_1_out2),
    .reg03_on_off(demultiplexer_1_out3), .reg04_on_off(demultiplexer_1_out4),
    .reg05_on_off(demultiplexer_1_out5), .reg06_on_off(demultiplexer_1_out6),
    .reg07_on_off(demultiplexer_1_out7), .reg08_on_off(demultiplexer_1_out8),
    .reg09_on_off(demultiplexer_1_out9), .reg10_on_off(demultiplexer_1_out10),
    .reg11_on_off(demultiplexer_1_out11), .reg12_on_off(demultiplexer_1_out12),
    .reg13_on_off(demultiplexer_1_out13), .reg14_on_off(demultiplexer_1_out14),
    .reg15_on_off(demultiplexer_1_out15), .reg16_on_off(demultiplexer_1_out16),
    .reg17_on_off(demultiplexer_1_out17), .reg18_on_off(demultiplexer_1_out18),
    .reg19_on_off(demultiplexer_1_out19), .reg20_on_off(demultiplexer_1_out20),
    .reg21_on_off(demultiplexer_1_out21), .reg22_on_off(demultiplexer_1_out22),
    .reg23_on_off(demultiplexer_1_out23), .reg24_on_off(demultiplexer_1_out24),
    .reg25_on_off(demultiplexer_1_out25), .reg26_on_off(demultiplexer_1_out26),
    .reg27_on_off(demultiplexer_1_out27), .reg28_on_off(demultiplexer_1_out28),
    .reg29_on_off(demultiplexer_1_out29), .reg30_on_off(demultiplexer_1_out30),
    .reg31_on_off(demultiplexer_1_out31), .reg01_out(reg01_out), .reg02_out(reg02_out),
    .reg03_out(reg03_out), .reg04_out(reg04_out), .reg05_out(reg05_out), .reg06_out(reg06_out),
    .reg07_out(reg07_out), .reg08_out(reg08_out), .reg09_out(reg09_out), .reg10_out(reg10_out),
    .reg11_out(reg11_out), .reg12_out(reg12_out), .reg13_out(reg13_out), .reg14_out(reg14_out),
    .reg15_out(reg15_out), .reg16_out(reg_16_val), .reg17_out(reg_17_val), .reg18_out(reg_18_val),
    .reg19_out(reg19_out), .reg20_out(reg20_out), .reg21_out(reg21_out), .reg22_out(reg22_out),
    .reg23_out(reg23_out), .reg24_out(reg24_out), .reg25_out(reg_20_val), .reg26_out(reg26_out),
    .reg27_out(reg27_out), .reg28_out(reg28_out), .reg29_out(reg29_out), .reg30_out(reg30_out),
    .reg31_out(reg_19_val), .write_data(Data), .in_1(clock));
  read_mux read_mux_1 (
    .reg01_out(reg01_out), .in_2(reg02_out), .in_3(reg03_out), .in_5(reg04_out), .in_6(reg05_out),
    .in_7(reg06_out), .in_8(reg07_out), .in_9(reg08_out), .in_10(reg09_out), .in_11(reg10_out),
    .in_12(reg11_out), .in_13(reg12_out), .in_14(reg13_out), .in_15(reg14_out), .in_16(reg15_out),
    .in_17(reg_16_val), .in_19(reg_17_val), .in_20(reg_18_val), .in_21(reg19_out), .in_22(reg20_out),
    .in_23(reg21_out), .in_24(reg22_out), .in_25(reg23_out), .in_26(reg24_out), .in_27(reg_20_val),
    .in_28(reg26_out), .in_29(reg27_out), .in_30(reg28_out), .in_31(reg29_out), .in_32(reg30_out),
    .in_33(reg_19_val), .read_data1(read_data1), .read_reg1(read_reg1), .read_data2(read_data2),
    .read_reg2(read_reg2));

  // Other names for the same wires on the sheet: clk = clock; reg16_out[31:0] = reg_16_val;
  //   reg17_out[31:0] = reg_17_val; reg18_out[31:0] = reg_18_val; reg25_out[31:0] = reg_20_val;
  //   reg31_out[31:0] = reg_19_val; write_data[31:0] = Data; write_en = write_enable; write_reg[4:0] = write_register

  // Notes on the sheet:
  //   RR1
  //   RR2
  //   RW
  //   WA
  //   WE
  //   ^
  //   Write
  //   $s0 Val
  //   Debug
  //   $s1 Val
  //   $s2 Val
  //   $ra Val
  //   Read
  //   $sp Val
  //   R1
  //   R2
endmodule

module reg_8 (
  input  [7:0] D,
  input  reg_on_off,
  input  clk,
  output [7:0] Q
);

  Register \reg  (.D(D), .en(reg_on_off), .clk(clk), .Q(Q));  // open: clr
endmodule
