// Logisim project regfile_harness_evolution.circ as structural Verilog: 1 circuit, main circuit main
module main (
  output [7:0] out_1,
  output [31:0] Reg_0_Value,
  output [31:0] Reg_1_Value,
  output [31:0] Reg_2_Value,
  output [31:0] Reg_3_Value,
  output [31:0] Reg_4_Value,
  output [31:0] Read_Data_1,
  output [31:0] Read_Data_2
);

  wire clock_1_out;
  wire [7:0] adder_1_out;
  wire [31:0] Write_Data;

  Clock clock_1 (.out(clock_1_out));
  Register register_1 (.D(adder_1_out), .en(1'b1), .clk(clock_1_out), .Q(out_1));  // open: clr
  Adder adder_1 (.a(8'h1), .b(out_1), .out(adder_1_out));  // open: cin, cout
  ROM #(.dataWidth(32)) rom_1 (.addr(out_1), .data(Write_Data));
  ROM #(.dataWidth(16)) rom_2 ();  // open: addr, data
endmodule
