// Logisim project bit_splitter.circ as structural Verilog: 1 circuit, main circuit bits_2_to_25
module bits_2_to_25 (
  input  [1:0] in_1,
  input  [3:0] in_2,
  input  [31:0] Low_2_bits,
  input  [31:0] High_2_bits,
  input  [31:0] Middle_2_bits,
  input  [31:0] Middle_4_bits,
  input  [31:0] Middle_8_bits,
  input  [31:0] in_8,
  input  [31:0] in_9,
  output out_10,
  output [1:0] out_11,
  output [1:0] out_12,
  output [1:0] out_13,
  output [1:0] out_14,
  output [3:0] out_15,
  output [7:0] out_16,
  output [15:0] Middle_16_bits,
  output [23:0] out_18
);


  assign Middle_16_bits = in_8[25:10];
  assign out_10 = in_1[0];
  assign out_11 = in_2[1:0];
  assign out_12 = Low_2_bits[1:0];
  assign out_13 = High_2_bits[31:30];
  assign out_14 = Middle_2_bits[25:24];
  assign out_15 = Middle_4_bits[25:22];
  assign out_16 = Middle_8_bits[25:18];
  assign out_18 = in_9[25:2];

  // Notes on the sheet:
  //   32-bits -> 24-bits
  //   Middle 24-bits
endmodule
