// Logisim project ram_toy_evolution.circ as structural Verilog: 1 circuit, main circuit toy
module toy (
  input  [1:0] Address,
  input  Write_Enable,
  input  clock,
  input  Write_Data,
  output Read_Data
);

  RAM #(.addrWidth(2), .dataWidth(1), .databus("bibus")) ram_1 (
    .addr(Address), .we(Write_Enable), .oe(1'b1), .clk(clock), .din(Write_Data), .dout(Read_Data));

  // Notes on the sheet:
  //   Address Bit-Width = N=2 = 2^2=4-Addresses
  //   Data Bit-Width = M=1
  //   NxM=2x1=<Address-Bits>x<Data-Bits>
endmodule
