// Logisim project rom_toy_evolution.circ as structural Verilog: 1 circuit, main circuit main
module main (
  input  [1:0] in_1,
  input  [1:0] in_2,
  input  [2:0] in_3,
  input  [2:0] in_4,
  input  [3:0] in_5,
  input  [3:0] in_6,
  input  [4:0] in_7,
  input  [4:0] in_8,
  output [1:0] out_9,
  output out_10,
  output [1:0] out_11,
  output out_12,
  output [1:0] out_13,
  output out_14,
  output [1:0] out_15,
  output out_16
);

  ROM #(.addrWidth(2), .dataWidth(1)) rom_1 (.addr(in_1));  // open: data
  ROM #(.addrWidth(3), .dataWidth(1)) rom_2 (.addr(in_3));  // open: data
  ROM #(.addrWidth(4), .dataWidth(1)) rom_3 (.addr(in_5));  // open: data
  ROM #(.addrWidth(5), .dataWidth(1)) rom_4 (.addr(in_7));  // open: data
  ROM #(.addrWidth(2), .dataWidth(2)) rom_5 (.addr(in_2), .data(out_9));
  ROM #(.addrWidth(3), .dataWidth(2)) rom_6 (.addr(in_4), .data(out_11));
  ROM #(.addrWidth(4), .dataWidth(2)) rom_7 (.addr(in_6), .data(out_13));
  ROM #(.addrWidth(5), .dataWidth(2)) rom_8 (.addr(in_8), .data(out_15));

  // Notes on the sheet:
  //   Data-Bits=M=1
  //   contents of rom_1 (hex, n*v repeats v):
  //   0 1
  //   contents of rom_2 (hex, n*v repeats v):
  //   0 1 0 1
  //   contents of rom_3 (hex, n*v repeats v):
  //   0 1 0 1
  //   contents of rom_4 (hex, n*v repeats v):
  //   0 1 0 1
  //   Address-Bits=N=2    =>    4-Addresses
  //   Address-Bits=N=3    =>    8-Addresses
  //   Data-Bits=M=1
  //   Address-Bits=N=4    =>    16-Addresses
  //   Data-Bits=M=1
  //   Address-Bits=N=5    =>    32-Addresses
  //   Data-Bits=M=1
  //   contents of rom_5 (hex, n*v repeats v):
  //   0 3
  //   contents of rom_6 (hex, n*v repeats v):
  //   0 1 2 3 0 1 2 3
  //   contents of rom_7 (hex, n*v repeats v):
  //   0 1 2 3 0 1 2 3 0 1 2 3 0 1 2 3
  //   contents of rom_8 (hex, n*v repeats v):
  //   0 0 1 1 2 2 3 3 0 0 1 1 2 2 3 3 0 0 1 1 2 2 3 3 0 0 1 1 2 2 3 3
  //   Address-Bits=N=2    =>    4-Addresses
  //   Data-Bits=M=2    =>    word-size=2-bit
  //   Address-Bits=N=3    =>    8-Addresses
  //   Data-Bits=M=2    =>    word-size=2-bit
  //   Address-Bits=N=4    =>    16-Addresses
  //   Data-Bits=M=2    =>    word-size=2-bit
  //   Address-Bits=N=5    =>    32-Addresses
  //   Data-Bits=M=2    =>    word-size=2-bit
endmodule
