// Logisim project 300_Register-File.circ as structural Verilog: 9 circuits, main circuit main
module _2x1_MUX (
  input  i0,
  input  i1,
  input  s,
  output d
);

  wire and_1_out, and_2_out, not_1_out;

  not not_1 (not_1_out, s);
  and and_1 (and_1_out, i0, not_1_out);
  and and_2 (and_2_out, i1, s);
  or or_1 (d, and_1_out, and_2_out);

  // Notes on the sheet:
  //   d=[i0 * (s0)'] + [i1 * s0]
endmodule

module _4x1_MUX (
  input  i0,
  input  i1,
  input  i2,
  input  i3,
  input  s1,
  input  s0,
  output d
);

  wire and_1_out, and_2_out, and_3_out, and_4_out, not_1_out, not_2_out;

  not not_1 (not_1_out, s1);
  and and_1 (and_1_out, i0, not_1_out, not_2_out);
  and and_2 (and_2_out, i1, not_1_out, s0);
  and and_3 (and_3_out, i2, s1, not_2_out);
  and and_4 (and_4_out, i3, s1, s0);
  not not_2 (not_2_out, s0);
  or or_1 (d, and_1_out, and_2_out, and_3_out, and_4_out);
endmodule

module main (
  input  [7:0] Input,
  input  in_2,
  input  [7:0] W_data,
  input  [1:0] W_addr,
  input  [1:0] R_addr,
  input  [7:0] Input_2,
  input  in_7,
  input  in_8,
  input  W_en,
  input  R_en,
  input  Tri_State_Buffer,
  input  in_12,
  input  in_13,
  input  [3:0] in_14,
  input  [1:0] in_15,
  input  in_16,
  input  [1:0] Input_3,
  input  Enable,
  output [7:0] Output,
  output [7:0] Output_2,
  output [7:0] Output_3,
  output [7:0] out_22,
  output [7:0] out_23,
  output [7:0] out_24,
  output out_25,
  output [7:0] out_26,
  output [7:0] out_27,
  output out_28,
  output out_29,
  output out_30,
  output [3:0] Output_4
);

  wire clock_1_out, clock_2_out, clock_3_out, clock_4_out, n2x4_decoder_2_d0, n2x4_decoder_2_d1,
       n2x4_decoder_2_d2, n2x4_decoder_2_d3, n2x4_decoder_west_1_d0, n2x4_decoder_west_1_d1,
       n2x4_decoder_west_1_d2, n2x4_decoder_west_1_d3;

  Clock clock_1 (.out(clock_1_out));
  _8_bit_reg u_8_bit_reg_1 (.\input (Input), .clk(clock_1_out), .\output (Output), .load(in_2));
  Clock clock_2 (.out(clock_2_out));
  _8_bit_reg u_8_bit_reg_2 (.\input (Input_2), .clk(clock_2_out), .\output (Output_2), .load(in_7));
  Clock clock_3 (.out(clock_3_out));
  _8_bit_reg u_8_bit_reg_3 (.\input (Input_2), .clk(clock_3_out), .\output (Output_3), .load(in_8));
  _1x2_decoder u_1x2_decoder_1 (.Enable(in_16), .Input(in_13), .d0(out_28), .d1(out_30));
  _2x4_decoder u_2x4_decoder_1 (
    .Enable(Enable), .Input(Input_3), .d0(Output_4[0]), .d1(Output_4[1]), .d2(Output_4[2]), .d3(Output_4[3]));
  _2x4_decoder u_2x4_decoder_2 (
    .Enable(W_en), .Input(W_addr), .d0(n2x4_decoder_2_d0), .d1(n2x4_decoder_2_d1), .d2(n2x4_decoder_2_d2),
    .d3(n2x4_decoder_2_d3));
  Clock clock_4 (.out(clock_4_out));
  assign out_25 = in_12 ? Tri_State_Buffer : 1'bz;  // Controlled_Buffer controlled_buffer_1
  BitSelector #(.width(4)) bitselector_1 (.in(in_14), .out(out_29), .sel(in_15));
  _8_bit_reg u_8_bit_reg_4 (.\input (W_data), .clk(clock_4_out), .\output (out_23), .load(n2x4_decoder_2_d0));
  _8_bit_reg u_8_bit_reg_5 (.\input (W_data), .clk(clock_4_out), .\output (out_24), .load(n2x4_decoder_2_d1));
  _8_bit_reg u_8_bit_reg_6 (.\input (W_data), .clk(clock_4_out), .\output (out_26), .load(n2x4_decoder_2_d2));
  _8_bit_reg u_8_bit_reg_7 (.\input (W_data), .clk(clock_4_out), .\output (out_27), .load(n2x4_decoder_2_d3));
  assign out_22 = n2x4_decoder_west_1_d0 ? out_23 : 8'bz;  // Controlled_Buffer controlled_buffer_2
  assign out_22 = n2x4_decoder_west_1_d1 ? out_24 : 8'bz;  // Controlled_Buffer controlled_buffer_3
  assign out_22 = n2x4_decoder_west_1_d2 ? out_26 : 8'bz;  // Controlled_Buffer controlled_buffer_4
  assign out_22 = n2x4_decoder_west_1_d3 ? out_27 : 8'bz;  // Controlled_Buffer controlled_buffer_5
  _2x4_decoder_west u_2x4_decoder_west_1 (
    .Enable(R_en), .Input(R_addr), .d0(n2x4_decoder_west_1_d0), .d1(n2x4_decoder_west_1_d1),
    .d2(n2x4_decoder_west_1_d2), .d3(n2x4_decoder_west_1_d3));

  // Notes on the sheet:
  //   4x8 register-file (<num-addresses>x<data-bits>)
  //   Encoder (Bit-selector)
endmodule

module _2_bit_Parallel_Load_Reg (
  input  i1,
  input  i0,
  input  load,
  input  clk,
  output q1,
  output q0
);

  wire multiplexer_1_out, multiplexer_2_out, not_1_out;

  not not_1 (not_1_out, load);
  Multiplexer multiplexer_1 (.in0(i1), .in1(q1), .out(multiplexer_1_out), .sel(not_1_out), .en(1'b1));
  Multiplexer multiplexer_2 (.in0(i0), .in1(q0), .out(multiplexer_2_out), .sel(not_1_out), .en(1'b1));
  D_Flip_Flop d_ff_1 (.clk(clk), .D(multiplexer_1_out), .Q(q1));  // open: Qn, preset, en, reset
  D_Flip_Flop d_ff_2 (.clk(clk), .D(multiplexer_2_out), .Q(q0));  // open: Qn, preset, en, reset

  // Notes on the sheet:
  //   2-bit Parallel-Load Register
endmodule

module _4_bit_Parallel_Load_Reg (
  input  i3,
  input  i2,
  input  i1,
  input  i0,
  input  load,
  input  clk,
  output q3,
  output q2,
  output q1,
  output q0
);

  wire multiplexer_1_out, multiplexer_2_out, multiplexer_3_out, multiplexer_4_out, not_1_out;

  not not_1 (not_1_out, load);
  Multiplexer multiplexer_1 (.in0(i3), .in1(q3), .out(multiplexer_1_out), .sel(not_1_out), .en(1'b1));
  Multiplexer multiplexer_2 (.in0(i2), .in1(q2), .out(multiplexer_2_out), .sel(not_1_out), .en(1'b1));
  D_Flip_Flop d_ff_1 (.clk(clk), .D(multiplexer_1_out), .Q(q3));  // open: Qn, preset, en, reset
  Multiplexer multiplexer_3 (.in0(i1), .in1(q1), .out(multiplexer_3_out), .sel(not_1_out), .en(1'b1));
  D_Flip_Flop d_ff_2 (.clk(clk), .D(multiplexer_2_out), .Q(q2));  // open: Qn, preset, en, reset
  Multiplexer multiplexer_4 (.in0(i0), .in1(q0), .out(multiplexer_4_out), .sel(not_1_out), .en(1'b1));
  D_Flip_Flop d_ff_3 (.clk(clk), .D(multiplexer_3_out), .Q(q1));  // open: Qn, preset, en, reset
  D_Flip_Flop d_ff_4 (.clk(clk), .D(multiplexer_4_out), .Q(q0));  // open: Qn, preset, en, reset

  // Notes on the sheet:
  //   4-bit Parallel-Load Register
endmodule

module _2x4_decoder (
  input  Enable,
  input  [1:0] Input,
  output d0,
  output d1,
  output d2,
  output d3
);

  Decoder #(.select(2)) decoder_1 (.out0(d0), .out1(d1), .out2(d2), .out3(d3), .sel(Input), .en(Enable));
endmodule

module _8_bit_reg (
  input  [7:0] \input ,
  input  clk,
  input  load,
  output [7:0] \output 
);

  wire not_1_out;

  Register register_1 (.D(\input ), .Q(\output ), .clk(clk), .clr(not_1_out));  // open: en
  not not_1 (not_1_out, load);
endmodule

module _2x4_decoder_west (
  input  Enable,
  input  [1:0] Input,
  output d0,
  output d1,
  output d2,
  output d3
);

  Decoder #(.select(2)) decoder_1 (.out0(d0), .out1(d1), .out2(d2), .out3(d3), .sel(Input), .en(Enable));
endmodule

module _1x2_decoder (
  input  Enable,
  input  Input,
  output d0,
  output d1
);

  Decoder decoder_1 (.out0(d0), .out1(d1), .sel(Input), .en(Enable));
endmodule
